// Logisim project IO选做1.circ as structural Verilog: 3 circuits, main circuit MulitiLetter
module MulitiLetter (
);

  wire b_out, c_out, d_out, driver_1_a, driver_1_b, driver_1_c, driver_1_d, driver_1_e, driver_1_f,
       driver_1_g, e_out, encoder_1_u, encoder_1_x, encoder_1_y, encoder_1_z, f_out;

  Button b (.out(b_out));
  Button c (.out(c_out));
  Button d (.out(d_out));
  Button e (.out(e_out));
  Button f (.out(f_out));
  Encoder encoder_1 (
    .b(b_out), .c(c_out), .d(d_out), .e(e_out), .f(f_out), .x(encoder_1_x), .y(encoder_1_y), .z(encoder_1_z),
    .u(encoder_1_u));
  Driver driver_1 (
    .in1(encoder_1_x), .in2(encoder_1_y), .in3(encoder_1_z), .in4(encoder_1_u), .g(driver_1_g),
    .f(driver_1_f), .a(driver_1_a), .b(driver_1_b), .e(driver_1_e), .d(driver_1_d), .c(driver_1_c));
  _7_Segment_Display u_7_segment_display_1 (
    .g(driver_1_g), .f(driver_1_f), .a(driver_1_a), .b(driver_1_b), .e(driver_1_e), .d(driver_1_d),
    .c(driver_1_c));  // open: dp
endmodule

module Encoder (
  input  b,
  input  c,
  input  d,
  input  e,
  input  f,
  output x,
  output y,
  output z,
  output u
);

  wire not_1_out, not_2_out;

  or or_1 (y, f, e, d, c);
  not not_1 (not_1_out, c);
  not not_2 (not_2_out, d);
  or or_2 (u, f, d, b);
  and and_1 (z, not_1_out, not_2_out);

  assign x = 1'b1;
endmodule

module Driver (
  input  in1,
  input  in2,
  input  in3,
  input  in4,
  output g,
  output f,
  output a,
  output b,
  output e,
  output d,
  output c
);

  wire and_1_out, and_2_out, and_3_out, and_4_out, and_5_out, and_6_out, and_7_out, and_8_out, and_9_out,
       and_10_out, and_11_out, and_12_out, and_13_out, and_14_out, and_15_out, and_16_out, and_17_out,
       and_18_out, and_19_out, and_20_out, and_21_out, and_22_out, and_23_out, and_24_out, and_25_out,
       and_26_out, and_27_out, and_28_out, and_29_out, and_30_out, and_31_out, and_32_out, and_33_out,
       and_34_out, and_35_out, not_1_out, not_2_out, not_3_out, not_4_out, not_5_out, not_6_out, not_7_out,
       not_8_out, not_9_out, not_10_out, not_11_out, not_12_out, not_13_out, not_14_out, not_15_out,
       not_16_out, not_17_out, not_18_out, not_19_out, not_20_out, not_21_out, not_22_out, not_23_out,
       not_24_out, not_25_out, not_26_out, not_27_out, not_28_out, not_29_out, not_30_out, not_31_out,
       not_32_out, not_33_out, not_34_out, not_35_out, not_36_out, not_37_out, not_38_out, not_39_out,
       not_40_out, not_41_out, not_42_out, not_43_out;

  not not_1 (not_1_out, in2);
  and and_1 (and_1_out, not_1_out, in3);
  and and_2 (and_2_out, in3, not_2_out);
  not not_2 (not_2_out, in4);
  not not_3 (not_3_out, in1);
  and and_3 (and_3_out, not_3_out, in2, not_4_out);
  not not_4 (not_4_out, in3);
  and and_4 (and_4_out, in1, not_5_out);
  not not_5 (not_5_out, in2);
  and and_5 (and_5_out, in1, in4);
  not not_6 (not_6_out, in3);
  and and_6 (and_6_out, not_6_out, not_7_out);
  not not_7 (not_7_out, in4);
  not not_8 (not_8_out, in1);
  and and_7 (and_7_out, not_8_out, in2, not_9_out);
  not not_9 (not_9_out, in3);
  and and_8 (and_8_out, in2, not_10_out);
  not not_10 (not_10_out, in4);
  and and_9 (and_9_out, in1, not_11_out);
  not not_11 (not_11_out, in2);
  and and_10 (and_10_out, in1, in3);
  not not_12 (not_12_out, in2);
  and and_11 (and_11_out, not_12_out, not_13_out);
  not not_13 (not_13_out, in4);
  not not_14 (not_14_out, in1);
  and and_12 (and_12_out, not_14_out, in3);
  not not_15 (not_15_out, in1);
  and and_13 (and_13_out, not_15_out, in2, in4);
  and and_14 (and_14_out, in2, in3);
  not not_16 (not_16_out, in2);
  and and_15 (and_15_out, in1, not_16_out, not_17_out);
  not not_17 (not_17_out, in3);
  and and_16 (and_16_out, in1, not_18_out);
  not not_18 (not_18_out, in4);
  not not_19 (not_19_out, in1);
  and and_17 (and_17_out, not_19_out, not_20_out);
  not not_20 (not_20_out, in2);
  not not_21 (not_21_out, in1);
  and and_18 (and_18_out, not_21_out, not_22_out, not_23_out);
  not not_22 (not_22_out, in3);
  not not_23 (not_23_out, in4);
  not not_24 (not_24_out, in2);
  and and_19 (and_19_out, not_24_out, not_25_out);
  not not_25 (not_25_out, in4);
  not not_26 (not_26_out, in1);
  and and_20 (and_20_out, not_26_out, in3, in4);
  not not_27 (not_27_out, in3);
  and and_21 (and_21_out, in1, not_27_out, in4);
  not not_28 (not_28_out, in2);
  and and_22 (and_22_out, not_28_out, not_29_out);
  not not_29 (not_29_out, in4);
  and and_23 (and_23_out, in3, not_30_out);
  not not_30 (not_30_out, in4);
  and and_24 (and_24_out, in1, in3);
  and and_25 (and_25_out, in1, in2);
  not not_31 (not_31_out, in1);
  not not_32 (not_32_out, in2);
  and and_26 (and_26_out, not_31_out, not_32_out, not_33_out);
  not not_33 (not_33_out, in4);
  not not_34 (not_34_out, in2);
  and and_27 (and_27_out, not_34_out, in3, in4);
  and and_28 (and_28_out, in2, not_35_out, in4);
  not not_35 (not_35_out, in3);
  and and_29 (and_29_out, in2, in3, not_36_out);
  not not_36 (not_36_out, in4);
  and and_30 (and_30_out, in1, not_37_out);
  not not_37 (not_37_out, in3);
  not not_38 (not_38_out, in1);
  and and_31 (and_31_out, not_38_out, not_39_out);
  not not_39 (not_39_out, in3);
  not not_40 (not_40_out, in1);
  and and_32 (and_32_out, not_40_out, in4);
  not not_41 (not_41_out, in3);
  and and_33 (and_33_out, not_41_out, in4);
  not not_42 (not_42_out, in1);
  and and_34 (and_34_out, not_42_out, in2);
  and and_35 (and_35_out, in1, not_43_out);
  not not_43 (not_43_out, in2);
  or or_1 (g, and_1_out, and_2_out, and_3_out, and_4_out, and_5_out);
  or or_2 (f, and_6_out, and_7_out, and_8_out, and_9_out, and_10_out);
  or or_3 (b, and_17_out, and_18_out, and_19_out, and_20_out, and_21_out);
  or or_4 (e, and_22_out, and_23_out, and_24_out, and_25_out);
  or or_5 (d, and_26_out, and_27_out, and_28_out, and_29_out, and_30_out);
  or or_6 (c, and_31_out, and_32_out, and_33_out, and_34_out, and_35_out);
  or or_7 (a, and_11_out, and_12_out, and_13_out, and_14_out, and_15_out, and_16_out);
endmodule
