// Logisim project IO选做3.circ as structural Verilog
// +
module _8bit_Adder (
  input  [7:0] in_1,
  input  in_2,
  input  [7:0] in_3,
  output [7:0] out_4,
  output out_5
);

  wire n4bit_adder_1_out_4;

  // Probe on in_1[3:0]
  // Probe on in_1
  _4bit_Adder u_4bit_adder_1 (
    .in_1(in_1[3:0]), .in_2(in_3[3:0]), .in_3(in_2), .out_4(n4bit_adder_1_out_4), .out_5(out_4[3:0]));
  // Probe on in_3
  _4bit_Adder u_4bit_adder_2 (
    .in_1(in_1[7:4]), .in_2(in_3[7:4]), .in_3(n4bit_adder_1_out_4), .out_4(out_5), .out_5(out_4[7:4]));
  // Probe on out_4
endmodule

module ALU (
  input  [7:0] in_1,
  input  [7:0] in_2,
  input  [4:0] in_3,
  input  in_4,
  input  in_5,
  output [7:0] out_6,
  output out_7
);

  wire [1:0] not_1_out;
  wire [7:0] au_1_out_6, cmp_1_out_4, lu_1_out_4, sf_1_out_4;
  wire [7:1] cmp_2_out_4;

  not not_1 (not_1_out[0], in_3[3]);
  not not_2 (not_1_out[1], in_3[4]);
  LU lu_1 (.in_1(in_2), .in_2(in_1), .S1S0(in_3[2:1]), .out_4(lu_1_out_4));
  AU au_1 (.in_1(in_1), .in_2(in_2), .Cin(in_3[0]), .Sub(in_3[1]), .in_5(in_3[2]), .out_6(au_1_out_6));  // open: out_7
  CMP cmp_1 (.in_1(in_2), .in_2(in_1), .in_3(in_3[2:1]), .out_4(cmp_1_out_4));
  SF sf_1 (.in_1(in_2), .in_2(3'b001), .in_3(in_3[2:1]), .out_4(sf_1_out_4));
  CMP cmp_2 (.in_1(in_1), .in_2(in_2), .in_3({in_5, in_4}), .out_4({cmp_2_out_4, out_7}));
  Multiplexer #(.select(2), .width(8)) multiplexer_1 (
    .in0(lu_1_out_4), .in1(au_1_out_6), .in2(cmp_1_out_4), .in3(sf_1_out_4), .out(out_6), .sel(not_1_out));  // open: en

  // Notes on the sheet:
  //   Instruction
  //   LU:  Logic Unit
  //   AU:  Arimatic Unit
  //   SF:  Shifter
  //   S3 S2 S1 S0
  //   Cin
  //   Shift bit
  //   0100 : A > B
  //   0101 : A = B
  //   0110 : A < B
  //   A
  //   B
  //   S1S0
  //   S2
  //   S3
  //   01XX : Perform Comparation Operation
  //   0000 : B
  //   00XX :  Perform shift operation
  //   0001 :  Logical left
  //   0010 :  Logical right
  //   0011 :  Arimatic right
  //   1000 : Y = A + B + Cin
  //   1001 : Y = A - B - Cin
  //   1010 : Y = A + 1
  //   1011 : Y = A  - 1
  //   10XX :  Perform arimatic operation
  //   1100 :  A && B   
  //   1101 :  A || B  
  //   1110 :  ~A  
  //   1111 : A XOR B 
  //   11XX :  Perform logic operation 
  //   Y
endmodule

// QA
module Quick_Adder (
  input  A0,
  input  A1,
  input  A2,
  input  A3,
  input  B0,
  input  B1,
  input  B2,
  input  B3,
  input  C0,
  output C1,
  output C2,
  output C3,
  output C4,
  output S0,
  output S1,
  output S2,
  output S3
);

  wire and_1_out, and_2_out, and_3_out, and_4_out, and_5_out, and_6_out, and_7_out, and_8_out, and_9_out,
       and_10_out, and_11_out, and_12_out, and_13_out, and_14_out, and_15_out, and_16_out, and_17_out,
       and_18_out, and_19_out, and_20_out, and_21_out, and_22_out, and_23_out, and_24_out, and_25_out,
       and_26_out, and_27_out, and_28_out, and_29_out, and_30_out, and_31_out, and_32_out, and_33_out,
       and_34_out, and_35_out, and_36_out, or_1_out, or_2_out, or_3_out, or_4_out, or_5_out, or_6_out,
       or_7_out, or_8_out, or_10_out, or_11_out, or_12_out, or_13_out, or_14_out, or_15_out, or_16_out,
       or_17_out, or_18_out, or_19_out, or_20_out, or_21_out, or_23_out, or_24_out, or_25_out, or_26_out,
       or_27_out, or_28_out, or_29_out, or_30_out, or_32_out, or_33_out, or_34_out, or_35_out;

  or or_1 (or_1_out, A0, B0);
  or or_2 (or_2_out, A0, B0);
  or or_3 (or_3_out, A0, B0);
  or or_4 (or_4_out, A0, B0);
  and and_1 (and_1_out, A0, B0);
  or or_5 (or_5_out, A0, B0);
  or or_6 (or_6_out, A0, B0);
  or or_7 (or_7_out, A0, B0);
  and and_2 (and_2_out, A0, B0);
  or or_8 (or_8_out, A0, B0);
  and and_3 (and_3_out, or_8_out, C0);
  and and_4 (and_4_out, A0, B0);
  and and_5 (and_5_out, or_1_out, C0);
  and and_6 (and_6_out, A0, B0);
  and and_7 (and_7_out, or_2_out, C0);
  and and_8 (and_8_out, A0, B0);
  and and_9 (and_9_out, or_3_out, C0);
  xor odd_parity_1 (S0, or_4_out, and_1_out, C0);
  and and_10 (and_10_out, A0, B0);
  and and_11 (and_11_out, or_5_out, C0);
  and and_12 (and_12_out, A0, B0);
  and and_13 (and_13_out, or_6_out, C0);
  and and_14 (and_14_out, A0, B0);
  and and_15 (and_15_out, or_7_out, C0);
  or or_9 (C1, and_2_out, and_3_out);
  or or_10 (or_10_out, A1, B1);
  or or_11 (or_11_out, and_4_out, and_5_out);
  or or_12 (or_12_out, A1, B1);
  or or_13 (or_13_out, and_6_out, and_7_out);
  or or_14 (or_14_out, A1, B1);
  or or_15 (or_15_out, and_8_out, and_9_out);
  or or_16 (or_16_out, A1, B1);
  and and_16 (and_16_out, A1, B1);
  or or_17 (or_17_out, and_10_out, and_11_out);
  or or_18 (or_18_out, A1, B1);
  or or_19 (or_19_out, and_12_out, and_13_out);
  or or_20 (or_20_out, A1, B1);
  or or_21 (or_21_out, and_14_out, and_15_out);
  and and_17 (and_17_out, A1, B1);
  and and_18 (and_18_out, or_10_out, or_11_out);
  and and_19 (and_19_out, A1, B1);
  and and_20 (and_20_out, or_12_out, or_13_out);
  and and_21 (and_21_out, A1, B1);
  and and_22 (and_22_out, or_14_out, or_15_out);
  xor odd_parity_2 (S1, or_16_out, and_16_out, or_17_out);
  and and_23 (and_23_out, A1, B1);
  and and_24 (and_24_out, or_18_out, or_19_out);
  and and_25 (and_25_out, A1, B1);
  and and_26 (and_26_out, or_20_out, or_21_out);
  or or_22 (C2, and_17_out, and_18_out);
  or or_23 (or_23_out, A2, B2);
  or or_24 (or_24_out, and_19_out, and_20_out);
  or or_25 (or_25_out, A2, B2);
  or or_26 (or_26_out, and_21_out, and_22_out);
  or or_27 (or_27_out, A2, B2);
  and and_27 (and_27_out, A2, B2);
  or or_28 (or_28_out, and_23_out, and_24_out);
  or or_29 (or_29_out, A2, B2);
  or or_30 (or_30_out, and_25_out, and_26_out);
  and and_28 (and_28_out, A2, B2);
  and and_29 (and_29_out, or_23_out, or_24_out);
  and and_30 (and_30_out, A2, B2);
  and and_31 (and_31_out, or_25_out, or_26_out);
  xor odd_parity_3 (S2, or_27_out, and_27_out, or_28_out);
  and and_32 (and_32_out, A2, B2);
  and and_33 (and_33_out, or_29_out, or_30_out);
  or or_31 (C3, and_28_out, and_29_out);
  or or_32 (or_32_out, A3, B3);
  or or_33 (or_33_out, and_30_out, and_31_out);
  or or_34 (or_34_out, A3, B3);
  and and_34 (and_34_out, A3, B3);
  or or_35 (or_35_out, and_32_out, and_33_out);
  and and_35 (and_35_out, A3, B3);
  or or_36 (C4, and_35_out, and_36_out);
  and and_36 (and_36_out, or_32_out, or_33_out);
  xor odd_parity_4 (S3, or_34_out, and_34_out, or_35_out);
endmodule

// AD
module _4bit_Adder (
  input  [3:0] in_1,
  input  [3:0] in_2,
  input  in_3,
  output out_4,
  output [3:0] out_5
);

  // Probe on in_1
  // Probe on in_2
  Quick_Adder quick_adder_1 (
    .A0(in_1[0]), .A1(in_1[1]), .A2(in_1[2]), .A3(in_1[3]), .B0(in_2[0]), .B1(in_2[1]), .B2(in_2[2]),
    .B3(in_2[3]), .C0(in_3), .C4(out_4), .S0(out_5[0]), .S1(out_5[1]), .S2(out_5[2]), .S3(out_5[3]));  // open: C1, C2, C3
  // Probe on out_5
endmodule

module LU (
  input  [7:0] in_1,
  input  [7:0] in_2,
  input  [1:0] S1S0,
  output [7:0] out_4
);

  wire [7:0] and_1_out, not_1_out, or_1_out, xor_1_out;

  assign and_1_out = in_1 & in_2;  // AND_Gate and_1, 8 bits wide
  assign or_1_out = in_1 | in_2;  // OR_Gate or_1, 8 bits wide
  assign not_1_out = ~in_1;  // NOT_Gate not_1, 8 bits wide
  assign xor_1_out = in_1 ^ in_2;  // XOR_Gate xor_1, 8 bits wide
  Multiplexer #(.select(2), .width(8)) multiplexer_1 (
    .in0(and_1_out), .in1(or_1_out), .in2(not_1_out), .in3(xor_1_out), .out(out_4), .sel(S1S0));  // open: en

  // Notes on the sheet:
  //   A
  //   B
  //   Y
endmodule

module SF (
  input  [7:0] in_1,
  input  [2:0] in_2,
  input  [1:0] in_3,
  output [7:0] out_4
);

  wire [7:0] shifter_1_out, shifter_2_out, shifter_3_out;

  Shifter shifter_1 (.in(in_1), .\dist (in_2), .out(shifter_1_out));
  Shifter #(.shift("lr")) shifter_2 (.in(in_1), .\dist (in_2), .out(shifter_2_out));
  Shifter #(.shift("ar")) shifter_3 (.in(in_1), .\dist (in_2), .out(shifter_3_out));
  Multiplexer #(.select(2), .width(8)) multiplexer_1 (
    .in0(in_1), .in1(shifter_1_out), .in2(shifter_2_out), .in3(shifter_3_out), .out(out_4), .sel(in_3));  // open: en
endmodule

module AU (
  input  [7:0] in_1,
  input  [7:0] in_2,
  input  Cin,
  input  Sub,
  input  in_5,
  output [7:0] out_6,
  output out_7
);

  wire xor_1_out;
  wire [7:0] multiplexer_1_out, xor_2_out, xor_3_out;

  xor xor_1 (xor_1_out, Cin, Sub);
  // Probe on in_1
  // Probe on in_2
  assign xor_2_out = in_2 ^ {8{Sub}};  // XOR_Gate xor_2, 8 bits wide
  Multiplexer #(.width(8)) multiplexer_1 (
    .in0(xor_2_out), .in1(xor_3_out), .out(multiplexer_1_out), .sel(in_5));  // open: en
  assign xor_3_out = 8'h1 ^ {8{Sub}};  // XOR_Gate xor_3, 8 bits wide
  // Probe on out_6
  _8bit_Adder u_8bit_adder_1 (.in_1(in_1), .in_2(xor_1_out), .in_3(multiplexer_1_out), .out_4(out_6), .out_5(out_7));

  // Notes on the sheet:
  //   A
  //   B
endmodule

module Regs (
  input  [7:0] in_1,
  input  R_W,
  input  CLK,
  input  [7:0] in_4,
  output [31:0] out_5,
  output [7:0] out_6,
  output [7:0] out_7
);

  wire and_1_out, and_2_out, and_3_out, and_4_out, decoder_1_out0, decoder_1_out1, decoder_1_out2,
       decoder_1_out3;

  Decoder_part #(.select(2)) decoder_1 (
    .out0(decoder_1_out0), .out1(decoder_1_out1), .out2(decoder_1_out2), .out3(decoder_1_out3),
    .sel(in_4[7:6]));  // open: en
  // Probe on in_1
  and and_1 (and_1_out, decoder_1_out0, R_W);
  and and_2 (and_2_out, decoder_1_out1, R_W);
  and and_3 (and_3_out, decoder_1_out2, R_W);
  and and_4 (and_4_out, decoder_1_out3, R_W);
  Register register_1 (.D(in_1), .en(and_1_out), .Q(out_5[7:0]), .clk(CLK));  // open: clr
  Register register_2 (.D(in_1), .en(and_2_out), .Q(out_5[15:8]), .clk(CLK));  // open: clr
  Register register_3 (.D(in_1), .en(and_3_out), .Q(out_5[23:16]), .clk(CLK));  // open: clr
  Register register_4 (.D(in_1), .en(and_4_out), .Q(out_5[31:24]), .clk(CLK));  // open: clr
  Multiplexer #(.select(2), .width(8)) multiplexer_1 (
    .in0(out_5[7:0]), .in1(out_5[15:8]), .in2(out_5[23:16]), .in3(out_5[31:24]), .out(out_7), .sel(in_4[3:2]));  // open: en
  Multiplexer #(.select(2), .width(8)) multiplexer_2 (
    .in0(out_5[7:0]), .in1(out_5[15:8]), .in2(out_5[23:16]), .in3(out_5[31:24]), .out(out_6), .sel(in_4[5:4]));  // open: en

  // Notes on the sheet:
  //   Data
  //   C-Reg
  //   SA
  //   SB
endmodule

module CPU (
  input  RST,
  output [4:0] out_2
);

  wire alu_1_out_7, and_1_out, clk_1_out_3, clk_1_out_4, clk_1_out_5, clk_1_out_6, clock_1_out, cu_1_out_7,
       cu_1_out_8, cu_1_out_9, cu_1_out_10, cu_1_out_13, cu_1_out_14;
  wire [6:0] adder_1_out;
  wire [7:0] A, B_I, cu_1_out_6, Out, R, R0, R1, R2, R3, ram_1_data, regs_1_out_7, Y;
  wire [15:0] rom_1_data;

  Clock clock_1 (.out(clock_1_out));
  // Probe on R0
  // Probe on R1
  // Probe on R2
  // Probe on R3
  CLK clk_1 (
    .CLK(clock_1_out), .Reset(RST), .out_3(clk_1_out_3), .out_4(clk_1_out_4), .out_5(clk_1_out_5),
    .out_6(clk_1_out_6));
  ROM #(.dataWidth(16)) rom_1 (.addr(cu_1_out_6), .data(rom_1_data));  // open: sel
  // Probe on R
  CU cu_1 (
    .in_2(clk_1_out_3), .in_3(RST), .in_4(rom_1_data), .in_5(clk_1_out_4), .out_7(cu_1_out_7),
    .out_8(cu_1_out_8), .out_9(cu_1_out_9), .out_10(cu_1_out_10), .out_11(out_2), .out_12(R),
    .out_6(cu_1_out_6), .out_13(cu_1_out_13), .out_14(cu_1_out_14), .in_1(alu_1_out_7));
  // Probe on Y
  // Probe on B_I
  // Probe on Out
  // Probe on A
  Regs regs_1 (
    .in_1(Y), .R_W(cu_1_out_7), .CLK(clk_1_out_5), .out_6(A), .out_7(regs_1_out_7), .in_4(R),
    .out_5({R3, R2, R1, R0}));
  Adder #(.width(7)) adder_1 (.a(7'b0110000), .b(ram_1_data[6:0]), .out(adder_1_out));  // open: cin, cout
  TTY #(.trigger("falling")) tty_1 (.data(adder_1_out), .clk(and_1_out));  // open: we, clr
  and and_1 (and_1_out, clk_1_out_6, cu_1_out_10);
  S_B_I s_b_i_1 (.in_1(regs_1_out_7), .imm(R[3:0]), .in_3(cu_1_out_8), .out_4(B_I));
  ALU alu_1 (
    .in_2(B_I), .in_1(A), .out_6(Out), .in_3(out_2), .in_4(cu_1_out_14), .in_5(cu_1_out_13),
    .out_7(alu_1_out_7));
  RAM #(.bus("separate")) ram_1 (
    .addr(A), .din(B_I), .data(ram_1_data), .str(cu_1_out_10), .clk(clk_1_out_6));  // open: sel, ld, clr
  Multiplexer #(.width(8)) multiplexer_1 (.in0(Out), .in1(ram_1_data), .out(Y), .sel(cu_1_out_9));  // open: en

  // Other names for the same wires on the sheet: Op[4:0] = out_2; Regs[31:0] = {R3, R2, R1, R0}

  // Notes on the sheet:
  //   CLK
  //   contents of rom_1 (hex, n*v repeats v):
  //   2001 2041 20c0 1084 4038 14f0 4 58 9003
  //   01XX : Perform Comparation Operation
  //   0100 : A > B
  //   0101 : A = B
  //   0110 : A < B
  //   0000 : B
  //   00XX :  Perform shift operation
  //   0001 :  Logical left
  //   0010 :  Logical right
  //   0011 :  Arimatic right
  //   1000 : Y = A + B + Cin
  //   1001 : Y = A - B - Cin
  //   1010 : Y = A + 1
  //   1011 : Y = A  - 1
  //   10XX :  Perform arimatic operation
  //   1100 :  A && B   
  //   1101 :  A || B  
  //   1110 :  ~A  
  //   1111 : A XOR B 
  //   11XX :  Perform logic operation 
endmodule

module CLK (
  input  CLK,
  input  Reset,
  output out_3,
  output out_4,
  output out_5,
  output out_6
);

  wire [1:0] counter_1_q;

  Counter #(.width(2), .max('h3)) counter_1 (.Q(counter_1_q), .clk(CLK), .clr(Reset));  // open: load, D, count, carry
  Decoder_part #(.select(2)) decoder_1 (
    .out0(out_3), .out1(out_4), .out2(out_5), .out3(out_6), .sel(counter_1_q));  // open: en
endmodule

module S_B_I (
  input  [7:0] in_1,
  input  [3:0] imm,
  input  in_3,
  output [7:0] out_4
);

  Multiplexer #(.width(8)) multiplexer_1 (.in0(in_1), .in1({4'b0000, imm}), .out(out_4), .sel(in_3));  // open: en

  // Notes on the sheet:
  //   B
  //   extend
endmodule

module Decoder (
  input  A,
  input  B,
  input  C,
  output RW,
  output SBI,
  output RM,
  output WM,
  output JP,
  output JZ,
  output JC
);

  wire and_1_out, and_2_out, and_3_out, and_4_out, not_1_out, not_2_out, not_3_out, not_4_out, not_5_out,
       not_6_out, not_7_out, not_8_out, not_9_out, not_10_out, not_11_out, not_12_out;

  not not_1 (not_1_out, A);
  not not_2 (not_2_out, B);
  not not_3 (not_3_out, A);
  not not_4 (not_4_out, B);
  not not_5 (not_5_out, C);
  not not_6 (not_6_out, A);
  not not_7 (not_7_out, A);
  not not_8 (not_8_out, C);
  not not_9 (not_9_out, B);
  not not_10 (not_10_out, C);
  not not_11 (not_11_out, B);
  not not_12 (not_12_out, C);
  and and_1 (and_1_out, not_1_out, not_2_out);
  and and_2 (and_2_out, not_3_out, C);
  and and_3 (and_3_out, not_4_out, C);
  and and_4 (and_4_out, A, not_5_out);
  and and_5 (RM, not_6_out, B, C);
  and and_6 (WM, not_7_out, B, not_8_out);
  and and_7 (JP, A, not_9_out, not_10_out);
  and and_8 (JZ, A, not_11_out, C);
  and and_9 (JC, A, B, not_12_out);
  or or_1 (RW, and_1_out, and_2_out);
  or or_2 (SBI, and_3_out, and_4_out);
endmodule

module PC (
  input  in_1,
  input  in_2,
  input  [4:0] in_3,
  input  in_4,
  input  [7:0] in_5,
  output [7:0] out_6
);

  wire and_1_out;
  wire [7:0] adder_1_out, bit_extender_1_out, multiplexer_1_out, multiplexer_2_out;

  assign bit_extender_1_out = {{4{1'b0}}, in_3[3:0]};  // Bit_Extender bit_extender_1
  Register register_1 (.D(multiplexer_2_out), .Q(out_6), .clk(in_1), .clr(in_2));  // open: en
  Multiplexer #(.width(8)) multiplexer_1 (
    .in0(8'h1), .in1(bit_extender_1_out), .out(multiplexer_1_out), .sel(in_4));  // open: en
  and and_1 (and_1_out, in_4, in_3[4]);
  Adder adder_1 (.a(out_6), .b(multiplexer_1_out), .out(adder_1_out));  // open: cin, cout
  Multiplexer #(.width(8)) multiplexer_2 (
    .in0(adder_1_out), .in1(in_5), .out(multiplexer_2_out), .sel(and_1_out));  // open: en
endmodule

module IR (
  input  [15:0] in_1,
  input  in_2,
  output [15:0] out_3
);

  Register #(.width(16)) register_1 (.D(in_1), .Q(out_3), .clk(in_2));  // open: en, clr
endmodule

module CU (
  input  in_1,
  input  in_2,
  input  in_3,
  input  [15:0] in_4,
  input  in_5,
  output [7:0] out_6,
  output out_7,
  output out_8,
  output out_9,
  output out_10,
  output [4:0] out_11,
  output [7:0] out_12,
  output out_13,
  output out_14
);

  wire and_1_out, id_1_out_6, or_1_out, or_2_out;
  wire [15:0] ir_1_out_3;

  or or_1 (or_1_out, in_1, id_1_out_6);
  and and_1 (and_1_out, or_1_out, or_2_out);
  IR ir_1 (.in_1(in_4), .in_2(in_5), .out_3(ir_1_out_3));
  PC pc_1 (.in_1(in_2), .in_2(in_3), .out_6(out_6), .in_4(and_1_out), .in_5(out_12), .in_3(out_11));
  ID id_1 (
    .in_1(ir_1_out_3), .out_2(out_7), .out_3(out_8), .out_4(out_9), .out_5(out_10), .out_6(id_1_out_6),
    .out_7(out_13), .out_8(out_14), .Op(out_11), .out_10(out_12));
  or or_2 (or_2_out, out_14, out_13, id_1_out_6);
endmodule

module ID (
  input  [15:0] in_1,
  output out_2,
  output out_3,
  output out_4,
  output out_5,
  output out_6,
  output out_7,
  output out_8,
  output [4:0] Op,
  output [7:0] out_10
);

  Decoder decoder_1 (
    .A(in_1[15]), .B(in_1[14]), .C(in_1[13]), .RW(out_2), .SBI(out_3), .RM(out_4), .WM(out_5), .JP(out_6),
    .JZ(out_7), .JC(out_8));

  assign Op = in_1[12:8];
  assign out_10 = in_1[7:0];

  // Notes on the sheet:
  //   Regs
endmodule

module Memory (
  input  [11:0] in_1,
  output [31:0] out_2
);

  wire decoder_1_out0, decoder_1_out1, decoder_1_out2, decoder_1_out3;

  Decoder_part #(.select(2)) decoder_1 (
    .out0(decoder_1_out0), .out1(decoder_1_out1), .out2(decoder_1_out2), .out3(decoder_1_out3),
    .sel(in_1[11:10]));  // open: en
  ROM #(.addrWidth(10), .dataWidth(16)) rom_1 (.addr(in_1[9:0]), .data(out_2[15:0]), .sel(decoder_1_out0));
  ROM #(.addrWidth(10), .dataWidth(16)) rom_2 (.addr(in_1[9:0]), .data(out_2[31:16]), .sel(decoder_1_out0));
  ROM #(.addrWidth(10), .dataWidth(16)) rom_3 (.addr(in_1[9:0]), .data(out_2[15:0]), .sel(decoder_1_out1));
  ROM #(.addrWidth(10), .dataWidth(16)) rom_4 (.addr(in_1[9:0]), .data(out_2[31:16]), .sel(decoder_1_out1));
  ROM #(.addrWidth(10), .dataWidth(16)) rom_5 (.addr(in_1[9:0]), .data(out_2[15:0]), .sel(decoder_1_out2));
  ROM #(.addrWidth(10), .dataWidth(16)) rom_6 (.addr(in_1[9:0]), .data(out_2[31:16]), .sel(decoder_1_out2));
  ROM #(.addrWidth(10), .dataWidth(16)) rom_7 (.addr(in_1[9:0]), .data(out_2[15:0]), .sel(decoder_1_out3));
  ROM #(.addrWidth(10), .dataWidth(16)) rom_8 (.addr(in_1[9:0]), .data(out_2[31:16]), .sel(decoder_1_out3));
endmodule

module CMP (
  input  [7:0] in_1,
  input  [7:0] in_2,
  input  [1:0] in_3,
  output [7:0] out_4
);

  wire comparator_1_eq, comparator_1_gt, comparator_1_lt, multiplexer_1_out;

  Comparator comparator_1 (.a(in_1), .b(in_2), .gt(comparator_1_gt), .eq(comparator_1_eq), .lt(comparator_1_lt));
  Multiplexer #(.select(2)) multiplexer_1 (
    .in0(comparator_1_gt), .in1(comparator_1_eq), .in2(comparator_1_lt), .out(multiplexer_1_out), .sel(in_3));  // open: in3, en
  assign out_4 = {{7{1'b0}}, multiplexer_1_out};  // Bit_Extender bit_extender_1
endmodule
