// Logisim project 存储器.circ as structural Verilog: 2 circuits, main circuit 位数扩展
module \位数扩展  (
  input  [11:0] in_1,
  input  in_2,
  output [31:0] out_3
);

  RAM #(.addrWidth(12), .dataWidth(16)) ram_1 (.addr(in_1), .data(out_3[15:0]), .sel(in_2));  // open: clk, ld, clr
  RAM #(.addrWidth(12), .dataWidth(16)) ram_2 (.addr(in_1), .data(out_3[31:16]), .sel(in_2));  // open: clk, ld, clr
  // Probe on out_3
endmodule

module \位数字数扩展  (
  input  [11:0] in_1,
  output [31:0] out_2
);

  wire decoder_1_out0, decoder_1_out1, decoder_1_out2, decoder_1_out3;

  Decoder #(.select(2)) decoder_1 (
    .out0(decoder_1_out0), .out1(decoder_1_out1), .out2(decoder_1_out2), .out3(decoder_1_out3),
    .sel(in_1[11:10]));  // open: en
  ROM #(.addrWidth(10), .dataWidth(16)) rom_1 (.addr(in_1[9:0]), .data(out_2[15:0]), .sel(decoder_1_out0));
  ROM #(.addrWidth(10), .dataWidth(16)) rom_2 (.addr(in_1[9:0]), .data(out_2[31:16]), .sel(decoder_1_out0));
  ROM #(.addrWidth(10), .dataWidth(16)) rom_3 (.addr(in_1[9:0]), .data(out_2[15:0]), .sel(decoder_1_out1));
  ROM #(.addrWidth(10), .dataWidth(16)) rom_4 (.addr(in_1[9:0]), .data(out_2[31:16]), .sel(decoder_1_out1));
  ROM #(.addrWidth(10), .dataWidth(16)) rom_5 (.addr(in_1[9:0]), .data(out_2[15:0]), .sel(decoder_1_out2));
  ROM #(.addrWidth(10), .dataWidth(16)) rom_6 (.sel(decoder_1_out2));  // open: addr, data
  // Probe on out_2
  ROM #(.addrWidth(10), .dataWidth(16)) rom_7 (.addr(in_1[9:0]), .data(out_2[15:0]), .sel(decoder_1_out3));
  ROM #(.addrWidth(10), .dataWidth(16)) rom_8 (.addr(in_1[9:0]), .data(out_2[31:16]), .sel(decoder_1_out3));

  // Notes on the sheet:
  //   contents of rom_1 (hex, n*v repeats v):
  //   0 0 ffe2 0 0 ffde
  //   contents of rom_2 (hex, n*v repeats v):
  //   a 4*0 12 ffac
endmodule
