// Logisim project 实验七 LED.circ as structural Verilog: 4 circuits, main circuit LED Counter
module LED (
);

  wire _1_out, _2_out, _3_out, _4_out, _5_out, driver_1_a, driver_1_b, driver_1_c, driver_1_d, driver_1_e,
       driver_1_f, driver_1_g, encoder_1_u, encoder_1_x, encoder_1_y, encoder_1_z, led_counter_1_out_6,
       led_counter_1_out_7, led_counter_1_out_8, led_counter_1_out_9, led_counter_1_out_10;

  Button _1 (.out(_1_out));
  Button _2 (.out(_2_out));
  Button _3 (.out(_3_out));
  Button _4 (.out(_4_out));
  Button _5 (.out(_5_out));
  LED_Counter led_counter_1 (
    .in_1(_1_out), .in_2(_2_out), .in_3(_3_out), .in_4(_4_out), .in_5(_5_out), .out_6(led_counter_1_out_6),
    .out_7(led_counter_1_out_7), .out_8(led_counter_1_out_8), .out_9(led_counter_1_out_9),
    .out_10(led_counter_1_out_10));
  LED_part led_1 (.in(led_counter_1_out_6));
  LED_part led_2 (.in(led_counter_1_out_7));
  LED_part led_3 (.in(led_counter_1_out_8));
  LED_part led_4 (.in(led_counter_1_out_9));
  LED_part led_5 (.in(led_counter_1_out_10));
  Encoder encoder_1 (
    .a(_1_out), .b(_2_out), .c(_3_out), .d(_4_out), .e(_5_out), .x(encoder_1_x), .y(encoder_1_y),
    .z(encoder_1_z), .u(encoder_1_u));
  Driver driver_1 (
    .in1(encoder_1_x), .in2(encoder_1_y), .in3(encoder_1_z), .in4(encoder_1_u), .g(driver_1_g),
    .f(driver_1_f), .a(driver_1_a), .b(driver_1_b), .e(driver_1_e), .d(driver_1_d), .c(driver_1_c));
  _7_Segment_Display u_7_segment_display_1 (
    .g(driver_1_g), .f(driver_1_f), .a(driver_1_a), .b(driver_1_b), .e(driver_1_e), .d(driver_1_d),
    .c(driver_1_c));  // open: dp
endmodule

module LED_Counter (
  input  in_1,
  input  in_2,
  input  in_3,
  input  in_4,
  input  in_5,
  output out_6,
  output out_7,
  output out_8,
  output out_9,
  output out_10
);

  or or_1 (out_6, in_1, in_2, in_3, in_4, in_5);
  or or_2 (out_7, in_2, in_3, in_4, in_5);
  or or_3 (out_8, in_3, in_4, in_5);
  or or_4 (out_9, in_4, in_5);

  assign out_10 = in_5;
endmodule

module Encoder (
  input  a,
  input  b,
  input  c,
  input  d,
  input  e,
  output x,
  output y,
  output z,
  output u
);

  or or_1 (y, e, d);
  or or_2 (z, c, b);
  or or_3 (u, e, c, a);

  assign x = 1'b0;
endmodule

module Driver (
  input  in1,
  input  in2,
  input  in3,
  input  in4,
  output g,
  output f,
  output a,
  output b,
  output e,
  output d,
  output c
);

  wire and_1_out, and_2_out, and_3_out, and_4_out, and_5_out, and_6_out, and_7_out, and_8_out, and_9_out,
       and_10_out, and_11_out, and_12_out, and_13_out, and_14_out, and_15_out, and_16_out, and_17_out,
       and_18_out, and_19_out, and_20_out, and_21_out, and_22_out, and_23_out, and_24_out, and_25_out,
       and_26_out, not_1_out, not_2_out, not_3_out, not_4_out, not_5_out, not_6_out, not_7_out, not_8_out,
       not_9_out, not_10_out, not_11_out, not_12_out, not_13_out, not_14_out, not_15_out, not_16_out,
       not_17_out, not_18_out, not_19_out, not_20_out, not_21_out, not_22_out, not_23_out, not_24_out,
       not_25_out, not_26_out, not_27_out, not_28_out, not_29_out, not_30_out, not_31_out, not_32_out,
       not_33_out, not_34_out, not_35_out, not_36_out, not_37_out, not_38_out, not_39_out, not_40_out,
       not_41_out, not_42_out, not_43_out, not_44_out, not_45_out, not_46_out, not_47_out, not_48_out,
       not_49_out, not_50_out, not_51_out, not_52_out;

  not not_1 (not_1_out, in1);
  and and_1 (and_1_out, not_1_out, not_2_out, in3);
  not not_2 (not_2_out, in2);
  not not_3 (not_3_out, in1);
  and and_2 (and_2_out, not_3_out, in2, not_4_out);
  not not_4 (not_4_out, in3);
  not not_5 (not_5_out, in1);
  and and_3 (and_3_out, not_5_out, in2, not_6_out);
  not not_6 (not_6_out, in4);
  not not_7 (not_7_out, in2);
  and and_4 (and_4_out, in1, not_7_out, not_8_out);
  not not_8 (not_8_out, in3);
  not not_9 (not_9_out, in1);
  not not_10 (not_10_out, in3);
  and and_5 (and_5_out, not_9_out, not_10_out, not_11_out);
  not not_11 (not_11_out, in4);
  not not_12 (not_12_out, in1);
  and and_6 (and_6_out, not_12_out, in2, not_13_out);
  not not_13 (not_13_out, in3);
  not not_14 (not_14_out, in1);
  and and_7 (and_7_out, not_14_out, in2, not_15_out);
  not not_15 (not_15_out, in4);
  and and_8 (and_8_out, in1, not_16_out, not_17_out);
  not not_16 (not_16_out, in2);
  not not_17 (not_17_out, in3);
  not not_18 (not_18_out, in1);
  not not_19 (not_19_out, in2);
  and and_9 (and_9_out, not_18_out, not_19_out, not_20_out);
  not not_20 (not_20_out, in4);
  not not_21 (not_21_out, in1);
  and and_10 (and_10_out, not_21_out, in3);
  not not_22 (not_22_out, in1);
  and and_11 (and_11_out, not_22_out, in2, in4);
  not not_23 (not_23_out, in2);
  and and_12 (and_12_out, in1, not_23_out, not_24_out);
  not not_24 (not_24_out, in3);
  not not_25 (not_25_out, in1);
  and and_13 (and_13_out, not_25_out, not_26_out);
  not not_26 (not_26_out, in2);
  not not_27 (not_27_out, in1);
  and and_14 (and_14_out, not_27_out, not_28_out, not_29_out);
  not not_28 (not_28_out, in3);
  not not_29 (not_29_out, in4);
  not not_30 (not_30_out, in2);
  and and_15 (and_15_out, not_30_out, not_31_out);
  not not_31 (not_31_out, in3);
  not not_32 (not_32_out, in1);
  and and_16 (and_16_out, not_32_out, in3, in4);
  not not_33 (not_33_out, in2);
  not not_34 (not_34_out, in3);
  and and_17 (and_17_out, not_33_out, not_34_out, not_35_out);
  not not_35 (not_35_out, in4);
  not not_36 (not_36_out, in1);
  and and_18 (and_18_out, not_36_out, in3, not_37_out);
  not not_37 (not_37_out, in4);
  not not_38 (not_38_out, in1);
  not not_39 (not_39_out, in2);
  not not_40 (not_40_out, in4);
  not not_41 (not_41_out, in1);
  not not_42 (not_42_out, in2);
  not not_43 (not_43_out, in1);
  not not_44 (not_44_out, in4);
  not not_45 (not_45_out, in1);
  not not_46 (not_46_out, in3);
  not not_47 (not_47_out, in2);
  not not_48 (not_48_out, in3);
  not not_49 (not_49_out, in2);
  and and_19 (and_19_out, not_49_out, not_50_out);
  not not_50 (not_50_out, in3);
  not not_51 (not_51_out, in1);
  and and_20 (and_20_out, not_51_out, in4);
  not not_52 (not_52_out, in1);
  and and_21 (and_21_out, not_52_out, in2);
  or or_1 (g, and_1_out, and_2_out, and_3_out, and_4_out);
  or or_2 (f, and_5_out, and_6_out, and_7_out, and_8_out);
  or or_3 (a, and_9_out, and_10_out, and_11_out, and_12_out);
  or or_4 (b, and_13_out, and_14_out, and_15_out, and_16_out);
  or or_5 (e, and_17_out, and_18_out);
  and and_22 (and_22_out, not_38_out, not_39_out, not_40_out);
  and and_23 (and_23_out, not_41_out, not_42_out, in3);
  and and_24 (and_24_out, not_43_out, in3, not_44_out);
  and and_25 (and_25_out, not_45_out, in2, not_46_out, in4);
  and and_26 (and_26_out, in1, not_47_out, not_48_out);
  or or_6 (c, and_19_out, and_20_out, and_21_out);
  or or_7 (d, and_22_out, and_23_out, and_24_out, and_25_out, and_26_out);
endmodule
