// Logisim project 实验六 汉字显示.circ as structural Verilog: 5 circuits, main circuit 例：机内转区位码
// 16*16字库
module \_16_16点阵字库  (
  input  [6:0] \区号 ,
  input  [6:0] \位号 ,
  output [31:0] D0,
  output [31:0] D1,
  output [31:0] D6,
  output [31:0] D3,
  output [31:0] D4,
  output [31:0] D5,
  output [31:0] D6_2,
  output [31:0] D7
);

  wire decoder_1_out0, decoder_1_out1, decoder_1_out2, decoder_1_out3;
  wire [1:0] subtractor_2_out_2;
  wire [6:0] multiplier_1_cout, multiplier_1_out, subtractor_1_out;
  wire [11:0] subtractor_2_out;
  wire [13:0] adder_1_out, bit_extender_1_out;

  Decoder #(.select(2), .enable("false")) decoder_1 (
    .out0(decoder_1_out0), .out1(decoder_1_out1), .out2(decoder_1_out2), .out3(decoder_1_out3),
    .sel(subtractor_2_out_2));
  ROM #(.addrWidth(12), .dataWidth(32)) rom_1 (.addr(subtractor_2_out), .data(D1), .sel(decoder_1_out0));
  ROM #(.addrWidth(14), .dataWidth(32)) rom_2 (.addr({subtractor_2_out_2, subtractor_2_out}), .data(D0));  // open: sel
  ROM #(.addrWidth(14), .dataWidth(32)) rom_3 (.addr({subtractor_2_out_2, subtractor_2_out}), .data(D4));  // open: sel
  Subtractor #(.width(7)) subtractor_1 (.a(\区号 ), .b(7'b0000001), .out(subtractor_1_out));  // open: bin, bout
  Multiplier #(.width(7)) multiplier_1 (
    .a(subtractor_1_out), .b(7'b1011110), .out(multiplier_1_out), .cout(multiplier_1_cout));  // open: cin
  ROM #(.addrWidth(12), .dataWidth(32)) rom_4 (.addr(subtractor_2_out), .data(D1), .sel(decoder_1_out1));
  ROM #(.addrWidth(14), .dataWidth(32)) rom_5 (.addr({subtractor_2_out_2, subtractor_2_out}), .data(D5));  // open: sel
  assign bit_extender_1_out = {{7{1'b0}}, \位号 };  // Bit_Extender bit_extender_1
  Adder #(.width(14)) adder_1 (
    .a({multiplier_1_cout, multiplier_1_out}), .b(bit_extender_1_out), .out(adder_1_out));  // open: cin, cout
  ROM #(.addrWidth(12), .dataWidth(32)) rom_6 (.addr(subtractor_2_out), .data(D1), .sel(decoder_1_out2));
  ROM #(.addrWidth(14), .dataWidth(32)) rom_7 (.addr({subtractor_2_out_2, subtractor_2_out}), .data(D6));  // open: sel
  ROM #(.addrWidth(14), .dataWidth(32)) rom_8 (
    .addr({subtractor_2_out_2, subtractor_2_out}), .data(D6_2));  // open: sel
  Subtractor #(.width(14)) subtractor_2 (
    .a(adder_1_out), .b(14'h1), .out({subtractor_2_out_2, subtractor_2_out}));  // open: bin, bout
  DotMatrix #(.inputtype("row"), .matrixcols(16), .matrixrows(16)) dotmatrix_1 (
    .row0(D0[15:0]), .row1(D0[31:16]), .row2(D1[15:0]), .row3(D1[31:16]), .row4(D6[15:0]), .row5(D6[31:16]),
    .row6(D3[15:0]), .row7(D3[31:16]), .row8(D4[15:0]), .row9(D4[31:16]), .row10(D5[15:0]),
    .row11(D5[31:16]), .row12(D6_2[15:0]), .row13(D6_2[31:16]), .row14(D7[15:0]), .row15(D7[31:16]));
  ROM #(.addrWidth(12), .dataWidth(32)) rom_9 (.addr(subtractor_2_out), .data(D1), .sel(decoder_1_out3));
  ROM #(.addrWidth(14), .dataWidth(32)) rom_10 (.addr({subtractor_2_out_2, subtractor_2_out}), .data(D3));  // open: sel
  ROM #(.addrWidth(14), .dataWidth(32)) rom_11 (.addr({subtractor_2_out_2, subtractor_2_out}), .data(D7));  // open: sel

  // Other names for the same wires on the sheet: D2[31:0] = D6; D6_t[31:0] = D6_2

  // Notes on the sheet:
  //   输入引脚区
  //   输入引脚区
  //   请勿增改引脚，请勿修改子电路封装
  //   contents of rom_1 (hex, n*v repeats v):
  //   7*0 1100000 3000380 0 0 2400240 0 100008 c000c00 440022 33003300 600038 3000e00 400000 1000200
  //   2400000 2400000 10001f0 800080 20803f8 500070 8200ff0 20807f8 7e007f0 3f007f0 800080 0 0 0 2200140
  //   20020000 18041ffc 18183ffc 10041004 180c0c18 30000c0 18180000 100008 800080 1200120 100008 63001c0
  //   20021004 900060 1000090 0 10480830 0 0 0 200020 230020c 1a00620 1800060 c00300 0 3c3c1818 3c00180
  //   2a001c0 2200220 2200220 600020 1b00090 33e84800 3f00090 163421c2 6b003f0 f80070 24101808 2000220
  //   1c401870 1400140 1c001c0 10080c30 1ff80ff0 263211c4 4100220 7f003e0 20043ffc 3ffc3ffc 14001c0
  //   1c001c0 11880000 0 0 1c001c0 800080 3ffc3ffc 16*0 3000700 cc00780 cc00780 3800180 18001fe0 cc00780
  //   1fe01fe0 cc00780 cc00780 1b1839b0 c601ce0 71e010c0 736011c0 70601020 730013f8 71b010e0 73f813f8
  //   71b010e0 71b010e0 799830f0 13841084 136411c4 136411c4 11c410c4 17f41004 133411e4 17f41004 136411c4
  //   11c41004 2c942464 2c642424 2c942464 2c942464 2c642424 2c8424f4 2c942464 2c9424f4 2c942464 2c942464
  //   29542624 21c21044 236211c4 236211c4 20c21044 27f21004 233211e4 27f21004 236211c4 21c21004 2eda1274 0
  //   0 20042004 20242004 2ff42024 28142004 2ff42024 21142104 21042104 22442044 22042204 20842084 0 0
  //   8001c0 2200770 8881ddc 8881ddc 4100e38 8881ddc 11143bbe 11543bfe 8881ddc 4100e38 8881ddc 11283bfc
  //   c300000 0 3c003c0 4200000 2200220 380c7c1e 12080c04 19000e0 700000 100008 8001000 0 800000 0 0 0
  //   80004 63003e0 3800080 66003c0 66003c0 1c000c0 c000ff0 66003c0 ff00ff0 66003c0 66003c0 0 0 30000c 0
  //   c003000 181807f0 41003e0 1c00080 c381fe0 63803e0 c701fc0 c181ff8 c181ff8 61c03f0 c181e3c 18003c0
  //   c001e0 c301e7c c001e00 180c380e e101c38 63003e0 c301fe0 e3803e0 c301fe0 c1807e8 318c3ffc c081e1c
  //   18083c1c 18c43dee c081e1c 380c7c1e 20183ff8 6000600 18003000 300030 800000 0 800180 0 6000e00 0
  //   6000e0 0 19800f0 0 6000e00 1800000 c00000 6000e00 1800380 7*0 800000 6*0 1000100 800080 400040 0
  //   1000100 1000080 8000000 10001000 7c00000 6007c0 1800300 8003c0 4600800 40c0818 1000200 1000206
  //   1f00200 1f60208 c00040 c60048 10101030 10131024 fc00000 fc60008 1000200 1060208 4000400 410040c
  //   800080 860088 2200020 2260028 24007c0 24607c8 4380400 43b0404 c9000a0 c9300a4 0 0 60008 3c0000
  //   3b0004 1000100 1080106 4300400 8080800 2700400 8600800 c600380 9240820 9230824 9240822 6180010
  //   61b0014 61a0015 3000000 310000c 3140008 0 10000c 140008 8200820 8230824 8220825 800080 f000000
  //   1f000400 13c01080 7000100 3400000 6000000 700020 10ec1050 800080 e00080 6000c0 4000400 64009c0
  //   8600800 64009c0 4000800 4000800 3e000000 8003c0 7c00100 1000100 11*0 ff80000 980004 600000 f8001e0
  //   800080 ffe0040 0 ff80000 200000 100010 1000100 1060108 1000200 1060208 4000200 4060208 4000200
  //   4060200 0 60008 2200220 2260228 6000c00 6060c08 ff80000 ff60008 2000200 2060208 100010 160008
  //   4000200 4060208 f0000f0 f0600e8 0 11080000 110e0008 ff0 60fe8 2000200 2060208 800080 ff80000 ff80000
  //   800100 300010 1000000 1060008 104000a 2000200 2060208 204020a 1ff80000 1ff60008 1ffa0004 0 60008
  //   40008 800080 860088 820085 0 1e00e00 c00040 180008 7f00000 2000000 4000400 0 0 7f00000 41ffc 7f0
  //   4400040 4400440 4000400 ffc0000 0 ffe0000 800080 ff80000 81ff8 c000000 430044 800080 1000000 8*0
  //   14001c0 e381ff0 e181ff8 1c001c0 e181ff8 20183ff8 c181e3c 63003e0 18003c0 c301e78 14001c0 380e0000
  //   e081c1c ff80ff8 63003e0 c181ffc e301fe0 8080ff8 11881ff8 1bc80e6c 18003c0 c081e1c 118823c4 c180630
  //   8*0 7200000 36000c0 80000 67003c0 3c00000 2600120 5b000e0 36001c0 7000100 e100200 a000400 c300000 0
  //   2200180 1c00000 0 33001e0 1f80000 fe00000 0 1000100 a100408 11000100 2200000 38*0 14001c0 e181ff8
  //   e381ff0 e181ff8 2300ff8 e181ff8 1ff80000 399c73ce 18381470 c181e3c 1e3c03e0 c341e18 2300ff8 380e0000
  //   c181e3c 63003e0 c181ffc e301fe0 63803e0 11881ff8 c081e1c 18003c0 c081e1c c181e3c c181e3c 318c7bde
  //   318c7bde 16001f00 18183c3c 6000f00 e300be0 198c3cf8 61803fc 15*0 3800000 38000e0 fe00000 ff00000
  //   ff80000 0 1200000 0 5c00000 f780000 2200000 f100000 ff80000 0 f780000 1c00000 ff80000 6e00000
  //   1e00000 ff00000 f380000 1800380 f380000 f780000 f780000 1ddc0000 1ddc0000 1f000000 1e3c0000 f000000
  //   3c00000 1e7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
  //   contents of rom_2 (hex, n*v repeats v):
  //   8*0 1000000 0 0 2400000 5*0 c0000 18000000 16*0 800000 0 0 0 10040000 7f00000 0 0 80000 800000 0 0 0
  //   c1803e0 0 600000 5*0 200000 0 18200000 180006 c003000 0 0 0 800000 1c00000 1c00000 200000 900000
  //   48003000 0 0 500000 0 40000 1c00000 38300000 800080 800080 3c00000 3c00000 c1803e0 1400080 1c00080 0
  //   0 800000 800000 0 0 0 800000 800000 3ffc0000 16*0 1000000 0 0 800000 5*0 8e00000 4200000 9*0 8080000
  //   8080000 8080000 8480000 5*8080000 11*10080000 10*c1803e0 0 0 5*10080000 11080000 4*10080000 16*0
  //   1800000 6*0 40000 20000000 5*0 20000 4*0 400000 38*0 7f80000 60000000 ff00000 0 0 1000100 26*0
  //   10000c0 800080 400180 0 0 800000 9*0 80000 2000000 2060008 0 60008 200000 30004 0 60008 2000000
  //   2060008 0 100000 800000 860008 0 60008 0 60008 0 30004 800000 830004 0 0 60008 0 30004 0 80000 0 0 0
  //   8000000 0 200000 230004 250002 0 30004 20000 0 100000 0 0 100000 0 f80000 fb0004 fa0000 800000 0
  //   4000000 800000 1000000 0 0 0 200000 0 800000 0 0 0 8000000 5*0 1000000 13*0 1ffe0000 0 3c0000 0
  //   400000 0 0 0 100000 1000000 1060008 2000000 2060008 2000000 2060008 1000000 1060008 0 60008 200000
  //   260008 0 60008 0 60008 0 60008 0 60008 2000000 2060008 0 60008 0 0 60008 0 60008 2000000 2060008 0 0
  //   0 2000000 0 0 60008 40000 0 60008 40000 0 60008 20000 0 60008 40000 0 60008 20000 12*0 400000 400000
  //   4*0 800000 0 0 0 30004 10*0 800000 0 0 800000 6*0 800000 8*0 380000 0 0 0 3e00000 21*0 400000 48*0
  //   800000 5*0 2200000 0 3c00000 0 6300000 38*0 300000 19*0 800000 25*0 800000 4400000 2000000 0 800000
  //   4400000 2000000 0 1000000 4400000 2000000 0 800000 4400000 2000000 0 800000 8800000 2000000 7c00000
  //   1000080 2800440 1000200 0 1000000 0 800000 800000 4400000 2000000 5*0 8000000 4000000 0 0 4000000
  //   1000000 0 1000000 0 0 0 200000 800000 0 1000000 400000 0 0 0 2000000 1000000 10080000 0 1000000 0 0
  //   0 2000000 0 3fe00000 8000000 2000000 0 0 1000000 100000 27*0 1000100 1800180 16*0 1000100 1000100
  //   1800180 1800180 1000100 1000100 1800180 1800180 1000100 1000100 1800180 1000100 1800180 1800180
  //   1000100 1800180 1000100 1000100 1800180 1000100 1800180 1800180 1000100 1800180 8*0 4*1000100
  //   4*1800180 4*1000100 1800180 1000100 1800180 1800180 1800180 1000100 1000100 1800180 1000100 1800180
  //   1800180 1800180 15*0 600000 6*0 80000 10000000 5*0 20000 4*0 200000 38*0 7f80000 60000000 ff00000 0
  //   0 1000100 26*0 400030 800080 1000600 0 600000 6*0 80000 10000000 5*0 20000 4*0 200000 38*0 7f80000
  //   60000000 ff00000 0 0 1000100 26*0 400030 800080 1000600 0 4*300c0ff0 381c0ff0 381c0ff0 300c0ff0
  //   3bdc0ff0 3ffc0ff0 3dfc0ff0 3ffc0ff0 3e7c0ff0 3f7c0ff0 3cfc0ff0 c423c423 2a543bdc 3bdc3bdc d5abc423
  //   294030c 39c030c fd6bfcf3 fce3fdf3 fc3ffe7f 3c00180 3c00180 fc3ffe7f e700420 f18ffbdf 7e00180
  //   f81ffe7f 66003c0 f99ffc3f 7e003c0 f81ffc3f 0 ffffffff 3c00180 1c380000 7e003c0 1800000 381c0ff0
  //   3ffc0ff0 4400000 400000 4000000 1800180 1800180 1800180 c000c0 1800180 1800180 1800180 4*0 1ff80000
  //   8001ffff 0 60002 600060 60004000 6000600 7e0000 700070 7e000000 e000e00 c000c c000c0 0 7000380 0
  //   300c300c 1800000 c000c00 c000c000 30003 0 80008000 10001 0 24001800 10081ff8 1c00000 3800000 4800000
  //   fb7fffff 1000100 38000000 6*0 1c00040 0 1e00060 0 3c001e0 3c000c0 0 0 1b00110 0 7000200 0 3e00120
  //   1e00180 0 0 1800180 0 1800180 0 1800180 1800180 0 0 7e00180 0 1800180 0 7e003c0 5a00180 0 0 3e001e00
  //   0 fc0078 0 1a001e00 ec0078 0 3cb0301 f800e0 0 7d00fe00 40004000 1ff00f0 3ec07580 10000 0 1d781900 0
  //   1800080 0 1df00900 f80098 0 0 2400040 0 2400200 0 4e00200 7700040 0 77fc01f8 12e00c0 0 7000300 0
  //   c8008c0 3c00180 0 1cde0000 1f80078 0 78000800 0 3cc01838 7801c00 0 0 2000200 0 400040 0 2000200
  //   600040 0 0 2000180 0 2000180 0 3000180 0 0 7ff80000 4000000 1000000 1bfe2004 1000000 0 0 1000100 0 0
  //   8000000 0 0 0 10000000 0 800000 0 0 0 800000 7ffc0000 0 1000000 80000 0 ff00020 20*0 7ffc3ffc 7f0000
  //   ff000000 3010301 80c080c0 5*0 ffffffff c000c000 ffffffff 30003 c000c000 30003 ffffffff 0 ffffffff 0
  //   8000ffff 80008000 1ffff 10001 80008000 10001 ffff 112*0 2f7e0004 7ffe0004 10401040 10401040 900090
  //   400040 1040200 10201020 440080 fffe0824 21e02018 4440440 5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
  //   contents of rom_3 (hex, n*v repeats v):
  //   0 0 0 180 0 4100410 c30 4400440 2600030 0 fe61c3 2400240 318c 4*0 400040 1000100 4000800 400020
  //   4800900 1200090 1000100 800080 2800280 500050 8800900 880048 7800700 f00070 800080 1400080 1ff8 0
  //   10040808 4100808 4000200 18181818 10041004 10041004 8000fc0 0 800040 800080 2400240 4000200 20022002
  //   408141c1 1000100 3800540 1ffc0000 3ffc0000 20881104 12042102 12202140 1000080 32006200 380026
  //   21800600 c20030 12242142 1800000 18180000 1c00080 800ff8 0 1000100 4800480 c000c00 9800b0 20022002
  //   19001900 1800180 58c0200 1400220 1352134c 4100808 7f00ff8 20042004 3ffc3ffc 48095005 10042002
  //   1ffc3ffe 20042004 3ffc3ffc 8080808 ff80ff8 2401998 30003c 6001e00 800080 4900080 17*0 3000300
  //   18000c0 6000c0 31801980 600060 18601860 3000300 18600cc0 7e00ce0 1b181b18 c600c60 30c03060 30303060
  //   36603360 30183018 33183318 30403040 331831b0 30f831b8 31981998 21822182 218220c2 20322062 2ff228c2
  //   20322032 26322732 20c22062 26322362 203221f2 44924492 44224422 44424422 44124412 45f24522 44124412
  //   44924492 44224422 44924492 44124412 44524452 40c140c1 418140c1 40314061 4ff144c1 40314031 46314731
  //   40c14061 46314361 40b14371 46d946d9 0 0 40024002 40024002 40024002 4c724a52 42224222 44224462
  //   41024102 44224222 42424242 40824082 0 10080000 800080 2200220 8880888 8500888 3200220 5080508
  //   a140a14 a540a54 8500820 2200140 5080208 a280428 c300c30 0 1800180 0 ff80220 1800180 2180100 cd8058c
  //   0 400040 2000200 1401ffc 800080 0 0 0 2000100 c180c18 1800180 c00060 300060 18c00cc0 300030 c300c30
  //   1800180 c300660 3f00670 30003000 1800 30006000 1ff80000 c0006 8000c0 12341224 7f00430 c0c0c18
  //   18001800 c0c0c0c c000c20 c000c20 183c1800 c180c18 1800180 c000c0 ce00dc0 c000c00 114c134c 8d008d0
  //   180c180c c000fe0 188c180c cc00fe0 180030 1800180 c080c08 6400c20 d680d68 36001c0 1800180 6000300
  //   6000600 6000c0 300030 1004 0 0 7e00060 6180618 c000c00 c600c60 ff00c30 1800180 7800cc0 6300630
  //   1800180 c000c0 7c00660 1800180 18c618c6 c300c30 6300630 6180618 6300630 6000600 1e00300 1800180
  //   c300c30 6200c10 d6808cc 1c00360 3200610 1800060 1000200 0 400020 fe61c3 9b00540 9480550 4000400
  //   8000800 100030 100018 1000080 1000080 c080608 6040504 4440244 4440244 200040 200040 4000c00 4000c00
  //   8100810 8100810 10000000 10000000 200040 200040 4000400 4000400 2800280 2800280 2a00220 2a00220
  //   1c800b80 1c800b80 4000400 4000400 c800b0 c800b0 100008 80008 80008 1000100 1000100 4000300 4000300
  //   4100420 10001000 14040a04 18082c04 12082104 6*10100810 1e00080 1e00080 1e00080 e01180 e01180 e01180
  //   10100810 10100810 10100810 800080 2e201430 16081608 22882104 1c80308 1280604 1240e02 9240924
  //   11221122 400040 400040 2f00200 4200e20 6040388 18202c20 60c0388 c080608 6040504 18040c0c 800140
  //   c019b0 4200620 11*0 2000100 1000180 1000100 800080 200010 100008 800080 800080 2200120 2100110
  //   2080208 2080208 fc000f8 fc000f8 800040 800040 1000080 1000080 80008 80008 2200220 2200220 400020
  //   400020 2200140 2200140 2000200 2000200 400020 400020 800140 800140 1000080 1000080 800040 4*1000080
  //   2000220 2000220 1000080 0 800140 8880490 4000200 10040808 10040808 10040808 2000200 2000200 2000200
  //   1000080 1000080 1000080 201040 201040 201040 10840888 10840888 10840888 2800040 10000000 4100200
  //   1400080 803ffc 800080 1000100 1ff80020 20 100010 40004 400020 4400440 4400440 4400420 8040804 200010
  //   100008 3ffe0880 800080 1000080 400020 100008 1080108 800080 8*0 43007f0 c380c70 c000c00 4300430
  //   c000c20 6000300 c180c18 1a2c1bec 1800180 ce00dc0 4300430 114c134c 8c808c8 41007f0 180c180c c180c18
  //   c000fe0 6000300 1800180 1800180 318c318c 36001c0 18003c0 e301c18 8*0 18c018c0 63006e0 1c00120
  //   c300660 c200600 8000800 6180618 6300630 3000300 66006c0 2200140 c300c30 1200320 2000200 6300630
  //   2400240 d800f60 6300630 3000300 6080608 19303118 2200140 19301110 1d5c194c 38*0 43007f0 c380c70
  //   c380c70 c000c00 8300430 c000c20 c200fe0 db00ff0 380070 d180c98 c980c98 c600cc0 8300430 114c134c
  //   c180c18 180c180c c180c18 c000fe0 18001800 1800180 3600320 318c318c 36001c0 c180c18 3d80678 318c318c
  //   318c318c 6180730 18d81d98 6180730 c000c 1b061b06 31803d8 15*0 c2006e0 6300630 6300660 6000600
  //   8600460 6080c00 40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
  //   电路功能：利用下图中给定的ROM器件实现汉字16*16点阵字库文件，不允许修改ROM地址数据位宽。
  //   图中有一个空白器件，表示少一个器件，请按照字扩展（容量扩展，地址线扩展）的方式利用第一行的存储器完成最终字库，
  //   输出引脚区
  //   contents of rom_4 (hex, n*v repeats v):
  //   280fffe 53fc5048 420fffe 4bfc4950 11001ffe 2007ffc 13f810a0 21242124 45084508 43f838a0 11081108
  //   3e442220 448845fc 48887dfc 20881080 8207efc 57fe7840 11081108 17f830a0 7f241424 20082008 1000100
  //   841080 104817fe 21082108 888f888 104017c0 10441040 4bfe4894 10a010a0 24401820 11083108 48a048a0
  //   44a044a0 547e4444 1df81150 7e7e1444 20002000 49007dc0 14101008 4017fe 840fbc0 200017fc 107ffc
  //   20003ffc 21102f70 48907ff0 104830a0 12041204 28822882 49107bfc 40244004 42043e04 22202210 8203ff8
  //   20a02010 20a02010 49203efe 27fc2048 10001ffe 22201140 11101110 6800880 17fc3040 8200820 1040100
  //   44427ffe 47e44404 27fc1048 111030a0 12203140 3ff82008 1000100 48407c40 20881040 14443444 40844084
  //   11fe1084 14441020 4a884c88 14081090 1441344 13f83208 2040200 fffe0104 52807f4c 10fe1084 104017c0
  //   480848a0 45fe7c00 49fe4400 24200420 25fe0400 257e2494 11180208 108013fe 48447c40 13fe1000 4bfc7c48
  //   11fc1028 17fc3048 11fc1028 8200800 7fe1044 5600300 10400840 20203fe 14500440 2a810a0 10001000 240010
  //   2200200 160213fe 40027ffe 1202fffe 121011f8 4a107df8 7d0221fe 340227fe 40027ffe 220223fe 200fffe
  //   4a024bfe 104037fc 1000100 40100 104017fc 420c4004 27fc1008 784007fc 207cff44 1000fffe 10007ffc
  //   3ffc0090 203ff8 4aa42a90 20881040 fffe0104 20802ffc 12241110 41244104 49fe7c94 11fe1094 4800c80
  //   24fe2444 21fe2094 920fffe 440fffe 1040100 17fe0844 10440940 20082008 27fe2044 7ffc0108 820fffe
  //   4bfc7c48 1ff01110 3ff82108 4a487e48 112411fe 10080840 17fc3444 27fc2444 21082108 20fe3f08 2087ffc
  //   10081ffe 12083208 14041020 fffe0104 40244804 20042040 49fe7d04 1110f0f8 8207ffc 40040804 52487910
  //   12100920 12100920 12081408 14881088 12083208 44427ffe 8907890 1050fe50 48404840 12081208 104037c0
  //   1007ffc 49087dfc 1d0811fc 10201ff0 8001800 401040 3ff82008 2000200 440fffe 10881080 4200400 10101010
  //   11101110 483f48 2007ffc 10881080 11000ff8 92905290 208017fc 120009fc 110811fc 3ffc0090 51127ffe
  //   48887c80 51045100 1ffe1004 18200ff0 10881080 12083208 4403ff8 44444444 110011e0 440fffe 1050fc50
  //   107efe40 49207d38 48407ffc 4a087a08 1df81108 509057fe 10d8f020 10101ff8 6c00100 9201110 48e04ffe
  //   7fc0208 111017fc 120813fc 14d81020 1501248 fe0884 3ff82008 24942790 4807ffc 22203ffc 4fffe 110411fe
  //   3ff80100 1dfc1128 13fc3248 4100400 54444b4c 2407e48 212421fe 4a227bfe 142013fe 5ff84010 51127ffe
  //   fe2223fe 54847c84 55fc1028 17fc0848 11fc2c28 2000200 22003ffe 10101ff0 48407c40 24202710 3c202710
  //   1ff81110 20401040 25fe1e54 102011e0 3ffc0090 48a04910 23c01100 23fe3f04 41044804 1102f70 ffe0804
  //   20a02ffe 10101010 511048a0 1128fd08 ff940918 8200820 4a084bfc 3d0820f8 1007ffc 49027ffe 510848f8
  //   49084508 10401048 11041104 22042200 43b83800 1040100 451028a0 3ef80000 1244327e 8200420 fe4429de
  //   fffc10a0 17fc30a0 ff081108 4bfe7c84 7ffc 1044fc20 8207ffc 17fe1224 17fe0a24 7ffe0804 3ffc1048
  //   3ff80920 1024fea8 51127ffe 9242a04 48507ff8 43ef8 3c2410a8 10483150 41027ffe 11b03040 4f807cfc
  //   1000100 2403fe0 13fe1004 5400920 48487bfc 28a01f7c ff240220 211427fe 274c2440 3f3e2120 15fc1104
  //   29fcfe28 20882080 17fc1048 164013fc 24440444 22481408 48884880 143017a8 88044002 17fe1024 48443f7e
  //   be4c4424 292427a4 12483248 9042402 28882fc8 20803ff8 8061440 820fffe 20001dfc 20403840 8203ff8
  //   407f60 110011e0 c00080 10000ffe 7f541054 3ff82008 4bf84a08 11fc2904 13f81208 11102108 11241104
  //   12241224 1110110c 12441244 20001000 28fc2884 1003ff8 fffe0104 12481240 11241120 10101010 50242010
  //   49fe4900 1ffe1004 14943110 fdfc1088 7f8422e0 10440840 211011f8 7ffc0288 108017fe 4a087ffc 20481c40
  //   1080100 241020 20482040 27fe2080 3ffc0090 51127ffe 3ffe0200 4bfe7c40 20441020 211010a0 124033fc
  //   7ffc0920 28442844 12fc1408 108810fc 20003ffc 200fffe 13fc1108 64842284 11701042 205023f8 204023f8
  //   fe201420 4a027bfe 40027ffe 10101ff0 fe8014fe fffe0104 13fc3248 24443ffe 4ffe7c44 20fe2084 2920fea0
  //   820fffe 201110 7ffe0100 41027ffe 2080100 22202220 fffe0104 24242420 10040ffe 140433fe 100010
  //   49240924 12483124 2104fefe 11103010 11243124 11103010 21103f10 11103010 20802080 11241124 290809fc
  //   928492fe 48907c10 c401030 840fffe 10400040 7e881408 3ff82108 4200223e 12283220 24fe0454 48907c90
  //   4400440 22102010 11f0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
  //   contents of rom_5 (hex, n*v repeats v):
  //   0 18002000 30000000 0 0 2200220 0 8800880 c001c0 0 38 2400240 5*0 400040 1000100 1000200 1000080
  //   2400480 2400120 1000100 800080 2800280 500050 8400880 1080088 7c00780 1f000f0 80 4100220 1800000
  //   1800000 20021004 2200410 8040400 18181818 10041004 10041004 4000800 18180000 3b001080 800080 4800480
  //   1ff80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
  //   contents of rom_6 (hex, n*v repeats v):
  //   18c618c6 4cc03fe 7fcc00ce 7ff800ac 2cff7f8e e1affff 7ffe0cc2 7ffe4862 19987f98 7ffe0186 fffc03ff
  //   7fff0238 3a781830 1bfe1ede ffc0c0c 7fff0332 19ff0982 183018fe ffc0c0c ffc0c0c 198c1d8e d180c18
  //   1b7e13de 14781fff 14701fff 1818181f 359919f9 7f7f7f60 1f8c1fee 189408d8 3d8831fc e6d0c6c 1830194e
  //   7fff0032 6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
  //   contents of rom_7 (hex, n*v repeats v):
  //   5*0 10041004 0 3300110 ffc0608 0 0 2400240 0 300030 10000800 cc00cc 44002200 400040 1000100 1000080
  //   400080 4800240 1200240 1000100 800080 28002f8 500050 8800840 880108 78007c0 f001f0 800080 4100808
  //   1800180 1800180 4100220 10042002 6000c04 18181818 10041004 10041004 4000400 1818 200010 800080
  //   1200120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
  //   contents of rom_8 (hex, n*v repeats v):
  //   0 c000c00 48004800 0 0 1c00140 0 11001100 4000e0 0 0 2400240 5*0 380060 e000300 400080 200 240 240
  //   1000100 f800080 3800280 10101fd0 ff00820 7f80208 7f007e0 7f003f0 ff8 808 180 180 2002 1400220
  //   1ffc1ffc 3c3c1818 c18180c 10041004 3000400 1818 c002e00 1ffc0080 4800480 0 0 c181004 c001200 c001200
  //   5*0 20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
  //   汉字显示验证区
  //   contents of rom_10 (hex, n*v repeats v):
  //   0 0 0 1800000 7f00000 8080808 c300000 6600330 10300c18 7ffe0000 3f800e00 2400240 318c0000 4*0 400040
  //   1000100 4000200 100020 9000480 900120 1000100 800080 2800280 500050 9000880 480088 7000780 7000f0
  //   800ff8 1400220 0 0 8080410 8081004 3000300 18181818 10041004 10041004 8000800 0 400020 800080
  //   2400240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
  //   contents of rom_11 (hex, n*v repeats v):
  //   0 0 3000 0 0 80 5*0 240 5*0 c 1800 7*0 1ff0 9*0 80 0 0 7f0 1004 c0 0 400 4*0 3e0 7*0 200 20c 0 60018
  //   30000c00 10*0 21c2 400 430 0 1c0 605e 2002 2002 0 0 3e0 80 80 7*0 80 80 3ffc 16*0 7b0 8*0 3ce6 1ef6
  //   9*0 9*808 11*1008 10*3e0 0 0 10*1008 23*0 4 2000 17*0 2000 c 0 3000 180 17*0 300048 9*0 7f8 2 ff0 9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
endmodule

module \_16_16姓名显示  (
);

  wire clock_1_out;
  wire [7:0] counter_1_q;
  wire [15:0] adder_1_out, negator_1_out, rom_1_data;
  wire [31:0] \n16_16点阵字库_1_d0 , \n16_16点阵字库_1_d1 , \n16_16点阵字库_1_d3 , \n16_16点阵字库_1_d4 , \n16_16点阵字库_1_d5 ,
       \n16_16点阵字库_1_d6 , \n16_16点阵字库_1_d6_2 , \n16_16点阵字库_1_d7 ;

  Counter counter_1 (.Q(counter_1_q), .clk(clock_1_out));  // open: load, D, count, carry, clr
  Clock clock_1 (.out(clock_1_out));
  Negator #(.width(16)) negator_1 (.in(16'ha0a0), .out(negator_1_out));
  ROM #(.dataWidth(16)) rom_1 (.addr(counter_1_q), .data(rom_1_data));  // open: sel
  Adder #(.width(16)) adder_1 (.a(rom_1_data), .b(negator_1_out), .out(adder_1_out));  // open: cin, cout
  \_16_16点阵字库  \u_16_16点阵字库_1  (
    .D0(\n16_16点阵字库_1_d0 ), .D1(\n16_16点阵字库_1_d1 ), .D6(\n16_16点阵字库_1_d6 ), .D3(\n16_16点阵字库_1_d3 ),
    .\区号 (adder_1_out[14:8]), .\位号 (adder_1_out[6:0]), .D4(\n16_16点阵字库_1_d4 ), .D5(\n16_16点阵字库_1_d5 ),
    .D6_2(\n16_16点阵字库_1_d6_2 ), .D7(\n16_16点阵字库_1_d7 ));
  DotMatrix #(.inputtype("row"), .matrixcols(16), .matrixrows(16)) dotmatrix_1 (
    .row0(\n16_16点阵字库_1_d0 [15:0]), .row1(\n16_16点阵字库_1_d0 [31:16]), .row2(\n16_16点阵字库_1_d1 [15:0]),
    .row3(\n16_16点阵字库_1_d1 [31:16]), .row4(\n16_16点阵字库_1_d6 [15:0]), .row5(\n16_16点阵字库_1_d6 [31:16]),
    .row6(\n16_16点阵字库_1_d3 [15:0]), .row7(\n16_16点阵字库_1_d3 [31:16]), .row8(\n16_16点阵字库_1_d4 [15:0]),
    .row9(\n16_16点阵字库_1_d4 [31:16]), .row10(\n16_16点阵字库_1_d5 [15:0]), .row11(\n16_16点阵字库_1_d5 [31:16]),
    .row12(\n16_16点阵字库_1_d6_2 [15:0]), .row13(\n16_16点阵字库_1_d6_2 [31:16]), .row14(\n16_16点阵字库_1_d7 [15:0]),
    .row15(\n16_16点阵字库_1_d7 [31:16]));

  // Notes on the sheet:
  //   contents of rom_1 (hex, n*v repeats v):
  //   b6fe c1e3 b6fe b6fe cee5 cbc4 c1f9 c8fd c1f5 d8b7 b3bd d0c5 cfa2 bfc6 d1a7 d3eb b9a4 b3cc d1a7 d4ba
endmodule

module \例_机内转区位码  (
  input  [15:0] GB2312,
  output [6:0] \区号 ,
  output [6:0] \位号 
);

  wire [15:0] negator_1_out;
  wire [15:7] adder_1_out;

  // Probe on GB2312
  Negator #(.width(16)) negator_1 (.in(16'ha0a0), .out(negator_1_out));
  // Probe on \区号 
  Adder #(.width(16)) adder_1 (
    .a(GB2312), .b(negator_1_out), .out({adder_1_out[15], \区号 , adder_1_out[7], \位号 }));  // open: cin, cout
  // Probe on \位号 

  // Notes on the sheet:
  //   请勿增改引脚，请勿修改子电路封装
  //   输入引脚区
  //   请在下方利用上方输入输出引脚的隧道标签信号构建电路，ctrl+d复制选择组件
  //   输出引脚区
  //   探测区
endmodule

// 32*32点阵字库
module \例_32_32点阵字库  (
  input  [6:0] \区号 ,
  input  [6:0] \位号 ,
  output [31:0] out_3,
  output [31:0] out_4,
  output [31:0] out_5,
  output [31:0] out_6,
  output [31:0] out_7,
  output [31:0] out_8,
  output [31:0] out_9,
  output [31:0] out_10,
  output [31:0] out_11,
  output [31:0] out_12,
  output [31:0] out_13,
  output [31:0] out_14,
  output [31:0] out_15,
  output [31:0] out_16,
  output [31:0] out_17,
  output [31:0] out_18,
  output [31:0] out_19,
  output [31:0] out_20,
  output [31:0] out_21,
  output [31:0] out_22,
  output [31:0] out_23,
  output [31:0] out_24,
  output [31:0] out_25,
  output [31:0] out_26,
  output [31:0] out_27,
  output [31:0] out_28,
  output [31:0] out_29,
  output [31:0] out_30,
  output [31:0] out_31,
  output [31:0] out_32,
  output [31:0] out_33,
  output [31:0] out_34
);

  wire [6:0] multiplier_1_cout, multiplier_1_out, subtractor_1_out;
  wire [13:0] adder_1_out, bit_extender_1_out, subtractor_2_out;

  ROM #(.addrWidth(14), .dataWidth(32)) rom_1 (.addr(subtractor_2_out), .data(out_3));  // open: sel
  ROM #(.addrWidth(14), .dataWidth(32)) rom_2 (.addr(subtractor_2_out), .data(out_4));  // open: sel
  ROM #(.addrWidth(14), .dataWidth(32)) rom_3 (.addr(subtractor_2_out), .data(out_5));  // open: sel
  ROM #(.addrWidth(14), .dataWidth(32)) rom_4 (.addr(subtractor_2_out), .data(out_6));  // open: sel
  ROM #(.addrWidth(14), .dataWidth(32)) rom_5 (.addr(subtractor_2_out), .data(out_7));  // open: sel
  ROM #(.addrWidth(14), .dataWidth(32)) rom_6 (.addr(subtractor_2_out), .data(out_8));  // open: sel
  ROM #(.addrWidth(14), .dataWidth(32)) rom_7 (.addr(subtractor_2_out), .data(out_9));  // open: sel
  ROM #(.addrWidth(14), .dataWidth(32)) rom_8 (.addr(subtractor_2_out), .data(out_10));  // open: sel
  Subtractor #(.width(7)) subtractor_1 (.a(\区号 ), .b(7'b0000001), .out(subtractor_1_out));  // open: bin, bout
  Multiplier #(.width(7)) multiplier_1 (
    .a(subtractor_1_out), .b(7'b1011110), .out(multiplier_1_out), .cout(multiplier_1_cout));  // open: cin
  ROM #(.addrWidth(14), .dataWidth(32)) rom_9 (.addr(subtractor_2_out), .data(out_11));  // open: sel
  ROM #(.addrWidth(14), .dataWidth(32)) rom_10 (.addr(subtractor_2_out), .data(out_12));  // open: sel
  ROM #(.addrWidth(14), .dataWidth(32)) rom_11 (.addr(subtractor_2_out), .data(out_13));  // open: sel
  ROM #(.addrWidth(14), .dataWidth(32)) rom_12 (.addr(subtractor_2_out), .data(out_14));  // open: sel
  ROM #(.addrWidth(14), .dataWidth(32)) rom_13 (.addr(subtractor_2_out), .data(out_15));  // open: sel
  ROM #(.addrWidth(14), .dataWidth(32)) rom_14 (.addr(subtractor_2_out), .data(out_16));  // open: sel
  ROM #(.addrWidth(14), .dataWidth(32)) rom_15 (.addr(subtractor_2_out), .data(out_17));  // open: sel
  ROM #(.addrWidth(14), .dataWidth(32)) rom_16 (.addr(subtractor_2_out), .data(out_18));  // open: sel
  assign bit_extender_1_out = {{7{1'b0}}, \位号 };  // Bit_Extender bit_extender_1
  Adder #(.width(14)) adder_1 (
    .a({multiplier_1_cout, multiplier_1_out}), .b(bit_extender_1_out), .out(adder_1_out));  // open: cin, cout
  ROM #(.addrWidth(14), .dataWidth(32)) rom_17 (.addr(subtractor_2_out), .data(out_19));  // open: sel
  ROM #(.addrWidth(14), .dataWidth(32)) rom_18 (.addr(subtractor_2_out), .data(out_20));  // open: sel
  ROM #(.addrWidth(14), .dataWidth(32)) rom_19 (.addr(subtractor_2_out), .data(out_21));  // open: sel
  ROM #(.addrWidth(14), .dataWidth(32)) rom_20 (.addr(subtractor_2_out), .data(out_22));  // open: sel
  ROM #(.addrWidth(14), .dataWidth(32)) rom_21 (.addr(subtractor_2_out), .data(out_23));  // open: sel
  ROM #(.addrWidth(14), .dataWidth(32)) rom_22 (.addr(subtractor_2_out), .data(out_24));  // open: sel
  ROM #(.addrWidth(14), .dataWidth(32)) rom_23 (.addr(subtractor_2_out), .data(out_25));  // open: sel
  ROM #(.addrWidth(14), .dataWidth(32)) rom_24 (.addr(subtractor_2_out), .data(out_26));  // open: sel
  Subtractor #(.width(14)) subtractor_2 (.a(adder_1_out), .b(14'h1), .out(subtractor_2_out));  // open: bin, bout
  ROM #(.addrWidth(14), .dataWidth(32)) rom_25 (.addr(subtractor_2_out), .data(out_27));  // open: sel
  ROM #(.addrWidth(14), .dataWidth(32)) rom_26 (.addr(subtractor_2_out), .data(out_28));  // open: sel
  ROM #(.addrWidth(14), .dataWidth(32)) rom_27 (.addr(subtractor_2_out), .data(out_29));  // open: sel
  ROM #(.addrWidth(14), .dataWidth(32)) rom_28 (.addr(subtractor_2_out), .data(out_30));  // open: sel
  ROM #(.addrWidth(14), .dataWidth(32)) rom_29 (.addr(subtractor_2_out), .data(out_31));  // open: sel
  ROM #(.addrWidth(14), .dataWidth(32)) rom_30 (.addr(subtractor_2_out), .data(out_32));  // open: sel
  ROM #(.addrWidth(14), .dataWidth(32)) rom_31 (.addr(subtractor_2_out), .data(out_33));  // open: sel
  ROM #(.addrWidth(14), .dataWidth(32)) rom_32 (.addr(subtractor_2_out), .data(out_34));  // open: sel
  ROM #(.addrWidth(14), .dataWidth(32)) rom_33 ();  // open: addr, data, sel
  DotMatrix #(.inputtype("row"), .matrixcols(32), .matrixrows(32), .dotshape("circle")) dotmatrix_1 (
    .row0(out_3), .row1(out_4), .row2(out_5), .row3(out_6), .row4(out_7), .row5(out_8), .row6(out_9),
    .row7(out_10), .row8(out_11), .row9(out_12), .row10(out_13), .row11(out_14), .row12(out_15),
    .row13(out_16), .row14(out_17), .row15(out_18), .row16(out_19), .row17(out_20), .row18(out_21),
    .row19(out_22), .row20(out_23), .row21(out_24), .row22(out_25), .row23(out_26), .row24(out_27),
    .row25(out_28), .row26(out_29), .row27(out_30), .row28(out_31), .row29(out_32), .row30(out_33),
    .row31(out_34));

  // Other names for the same wires on the sheet: D0[31:0] = out_3; D1[31:0] = out_4; D2[31:0] = out_5;
  //   D3[31:0] = out_6; D4[31:0] = out_7; D5[31:0] = out_8; D6[31:0] = out_9; D7[31:0] = out_10; D8[31:0] = out_11;
  //   D9[31:0] = out_12; D10[31:0] = out_13; D11[31:0] = out_14; D12[31:0] = out_15; D13[31:0] = out_16;
  //   D14[31:0] = out_17; D15[31:0] = out_18; D16[31:0] = out_19; D17[31:0] = out_20; D18[31:0] = out_21;
  //   D19[31:0] = out_22; D20[31:0] = out_23; D21[31:0] = out_24; D22[31:0] = out_25; D23[31:0] = out_26;
  //   D24[31:0] = out_27; D25[31:0] = out_28; D26[31:0] = out_29; D27[31:0] = out_30; D28[31:0] = out_31;
  //   D29[31:0] = out_32; D30[31:0] = out_33; D31[31:0] = out_34

  // Notes on the sheet:
  //   contents of rom_1 (hex, n*v repeats v):
  //   281*0 ffffffff 272*0 60000000 202*0 18000 3c000 0 0 18000 3c000 0 0 18000 3c000 8*0 18000 18000
  //   3c000 3c000 18000 18000 3c000 3c000 18000 18000 3c000 18000 3c000 3c000 18000 3c000 18000 18000
  //   3c000 18000 3c000 3c000 18000 3c000 8*0 4*18000 4*3c000 4*18000 3c000 18000 3c000 3c000 3c000 18000
  //   18000 3c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
  //   contents of rom_2 (hex, n*v repeats v):
  //   150*0 1c000 9*18000 121*0 ffffffff 269*0 10000 0 60000000 60000000 202*0 3c000 3c000 0 0 3c000 3c000
  //   0 0 3c000 3c000 8*0 24*3c000 8*0 24*3c000 587*0 8000 11*0 2000 124*0 8000 28*0 8000 291*0 400000
  //   742*0 1000 189*0 80 822*0 10000 654*0 40000 50*0 20000 64*0 4000 252*0 20000 56*0 40000 51*0 2000
  //   74*0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
  //   contents of rom_3 (hex, n*v repeats v):
  //   150*0 1ffc00 9*3ffc00 59*0 ff000 26*0 7ff0 0 ffe0000 30*0 10000 109*0 1c0000 144*0 60000006 0
  //   60000006 13*0 40000002 38000 0 60000000 e0000000 15*0 181800 0 0 0 e6000 182*0 3c000 3c000 0 0 3c000
  //   3c000 0 0 3c000 3c000 8*0 24*3c000 8*0 24*3c000 581*0 1800 1801800 8100 3000 60000 c00 c000 383800
  //   700002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
  //   contents of rom_4 (hex, n*v repeats v):
  //   11*0 c3000 5*0 40 2000000 10 8000000 80 0 1ff0 100000 1ff0 f80000 1fff0 fff8000 1ffe0 7ff0000 18*0
  //   800 3800 13*0 10000 18000 0 c00000 c20000 0 18000 0 0 0 400 3e000 0 10000 10000 13*0 18000 57*0
  //   10*f00f00 34*0 c00000 24*0 3ffe00 26*0 7ff0 1800000 ffe0000 0 0 300 26*0 1c0 18000 3c00000 49*0 1c0
  //   57*0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
  //   contents of rom_5 (hex, n*v repeats v):
  //   8*0 40000 0 0 c3000 0 20 3c00000 1820 3c70000 e0 6000000 30 18000000 198 19800000 1800 100000 1830
  //   d80000 1ffe0 7ff8000 1ffc0 7ff0000 18000 0 0 0 18000 12*0 7e000 3c00 7c00 6*0 30000 c000 10 4000000
  //   0 0 0 18000 ff000 800000 1c00000 1c70000 2000000 18000 18000018 0 c000 7000c00 ff800 0 18000 18000
  //   3c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
  //   contents of rom_6 (hex, n*v repeats v):
  //   4*0 1ff800 300c00 181800 0 70000 0 0 c3000 0 c0 3c00000 20c0 3cf8000 1c0 3000000 30 c000000 1b0
  //   18c00000 1800 100000 1bf0 d80000 180c0 3018000 1ffc0 3ff0000 18000 0 0 0 18000 c000030 7ffff80
  //   1ffffff8 4*0 180 18000 8060 0 0 3ffc00 6e00 ce00 5*0 300 30000 c000 70 7800000 0 0 0 18000 1e7800
  //   7e00000 1c0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
  //   contents of rom_7 (hex, n*v repeats v):
  //   4*0 3ffc00 1c3800 3c3c00 0 60000 0 0 c3000 0 180 3c00000 6180 3cf8000 180 1800000 60 c000000 330
  //   cc00000 1800 100000 1be0 d80000 18180 1818000 1ff80 1ff0000 18000 80 38000 18000 3c000 c000030
  //   3ffff80 ffffff0 0 3c000 0 1800180 180 18000 c060 18 0 780e00 ce00 cc00 5*0 300 30000 c000 3e0
  //   3e00000 0 1c00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
  //   contents of rom_8 (hex, n*v repeats v):
  //   5*0 77000 3c3c00 0 60000 0 0 c3000 0 180 3c00000 c180 3c78000 300 c00000 60 6000000 320 c600000 1800
  //   100000 1a00 d80000 18180 1c18000 1ff00 ff0000 18000 30001c0 7c000 3c000 3c000 6000060 3800380
  //   1c00380 1800180 1ff800 0 3c003c0 180 18000 180c0 70 0 1c00300 c000 c000 5*0 600 30000 c000 1f00
  //   7c0000 0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
  //   contents of rom_9 (hex, n*v repeats v):
  //   5*0 3c000 181800 0 c0000 0 0 c3000 0 300 c00000 1c300 c30000 600 600000 c0 6000000 660 6600000 1800
  //   100000 1a00 d80000 18300 c18000 1ff00 ff0000 18000 1800380 7c000 7e000 66000 6000060 1c00080 1c00380
  //   1800180 7ffe00 3fffc0 3e007c0 300 18000 380c0 e0 7e000 3800180 c000 c000 0 1800f80 0 0 0 c00 30038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
  //   contents of rom_10 (hex, n*v repeats v):
  //   5*0 18000 0 0 c0300 0 0 c3000 0 3c0 1800000 1e3c0 1830000 400 600000 c0 3000000 660 6300000 1800
  //   100000 1a00 d80000 18600 618000 1fe00 7f0000 18000 c00700 7c000 3c000 66000 30000c0 e000c0 1c00380
  //   1800180 e00700 7fffc0 3e007c0 300 18000 30180 1c0 3ffc00 30000c0 18000 1c000 0 7803fe0 0 0 0 c00
  //   301f0 f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
  //   contents of rom_11 (hex, n*v repeats v):
  //   8*0 187f80 0 0 c3000 0 7c0 1000000 1f7c0 1060000 400 600000 180 3000000 cc0 3300000 1800 100000 1a00
  //   d80000 18600 618000 1fc00 7f0000 18000 600e00 38000 3c000 63000 30000c0 e00040 1c00380 1800180
  //   c00300 e00000 3c003c0 300 18000 60180 380 f00f00 6000060 18000 1c000 ffffff0 e007070 f00000 0 0 1800
  //   30f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
  //   contents of rom_12 (hex, n*v repeats v):
  //   7*0 31c00 1ff700 0 0 c3000 0 3c0 2000000 1f3c0 20c0000 400 600000 180 1800000 cc0 3180000 1800
  //   100000 1a00 d80000 18c00 318000 1fc00 3f0000 18000 301c00 0 0 c3000 1800180 700000 1c00380 1800180
  //   1c00380 1800000 800100 600 18000 60300 700 1c00380 e000060 18000 1c000 1ffffff8 c00c030 3fc0000
  //   800700 f00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
  //   contents of rom_13 (hex, n*v repeats v):
  //   7*0 71c00 360600 0 0 c3000 0 3c0 4000000 1e3c0 4180000 400 600000 300 1800000 1980 1980000 1800
  //   100000 1a00 d80000 18c00 318000 1fc00 3f0000 18000 183800 0 0 c1800 1800180 780000 1c00380 1800180
  //   1800180 3800000 0 600 18000 c0300 e00 38001c0 c000030 18000 7f000 0 1c018038 70f0018 7803fc0 3fc07f0
  //   1fff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
  //   contents of rom_14 (hex, n*v repeats v):
  //   0 0 0 3c000 0 0 0 73800 200600 0 1e00000 c3000 0 80 0 4080 0 400 600000 300 c00000 1980 18c0000 1800
  //   100000 1a00 d80000 18800 318000 1f800 3f0000 18000 c7000 0 0 181800 c00300 380000 1c00380 1800180
  //   1800180 3000000 0 600 18000 c0600 1c00 60000e0 c000030 18000 fb800 0 1c030038 c03c030 e0070e0
  //   70f1e00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
  //   contents of rom_15 (hex, n*v repeats v):
  //   0 0 0 7e000 0 0 0 63800 400c00 0 7f80008 c3000 e03c070 4*0 400 600000 600 c00000 3300 cc0000 1800
  //   100000 1a00 d80000 19800 118000 1f800 3f0000 7ffffe0 6e000 0 0 181800 c00300 1c0000 1c00380 1800180
  //   1800180 3000000 0 c00 18000 180600 3800 e000070 1c038030 18000 198c00 0 c070030 1800f0e0 c00c030
  //   c03b0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
  //   contents of rom_16 (hex, n*v repeats v):
  //   0 0 0 ff000 0 0 0 e3000 800c00 0 e1f0018 c3000 1f07c0f8 4*0 400 600000 600 600000 3300 c60000 1800
  //   100000 1a00 d80000 19800 198000 1f800 3f0000 7ffffe0 3c000 0 0 300c00 600600 1e0000 1c00380 1800180
  //   1800180 3ffff80 0 c00 18000 180c00 6000 c000030 1807c030 18000 198c00 0 e0e0070 3fc0 1801c030
  //   1801e00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
  //   contents of rom_17 (hex, n*v repeats v):
  //   0 0 0 ff000 0 0 0 c7000 1800 ffffffff 1803e030 c3000 1f07e1f8 4*0 400 600000 c00 600000 6600 460000
  //   1800 100000 1a00 d80000 19800 198000 1f800 3f0000 18000 38000 ffffff0 0 300c00 600600 e0000 1c00380
  //   1800180 1800180 3ffffc0 0 c00 18000 301c00 c000 18000018 1807e038 18000 198c00 1ffffff8 7fc01e0 f00f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
  //   contents of rom_18 (hex, n*v repeats v):
  //   0 0 0 ff000 0 0 0 c6000 1000 0 10007fe0 c3000 1f07c0f8 4*0 400 600000 600 600000 3300 c60000 1800
  //   100000 1a00 d80000 19800 198000 1f800 3f0000 18000 3c000 7ffffe0 0 600600 300c00 70000 1c00380
  //   1800180 1800180 3ffff80 0 1800 18000 301800 18000 18000018 1807c030 18000 198c00 0 1f00180 3fc0000
  //   1c030030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
  //   contents of rom_19 (hex, n*v repeats v):
  //   0 0 0 fe000 0 0 0 186000 3000 0 20000fc0 c3000 e03c0f0 4*0 400 600000 600 c00000 3300 cc0000 1800
  //   100000 1a00 d80000 19800 118000 1f800 3f0000 18000 6e000 0 0 600600 300c00 60000 1c00380 1800180
  //   1800180 3000000 0 181800 18000 603800 30000 10000008 1c03c030 18000 199c00 0 0 70f0018 c0e0070
  //   e03b800 30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
  //   contents of rom_20 (hex, n*v repeats v):
  //   0 0 0 7e000 0 0 0 18c000 42000 0 100 c3000 5*0 400 600000 300 c00000 3180 18c0000 1800 100000 1a00
  //   d80000 18800 318000 1f800 3f0000 18000 c7000 0 0 c00300 181c00 c0000 1c00380 1800180 1800180 3000000
  //   0 3c1800 18000 603000 60000 0 c000030 18000 db800 0 0 c03c030 7bc01e0 7ff1ff0 1ffffff0 3f0000 f800 1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
  //   contents of rom_21 (hex, n*v repeats v):
  //   7*0 10c000 36000 0 0 c3000 5*0 400 600000 300 1800000 1980 1980000 1800 100000 1a00 d80000 18c00
  //   318000 1fc00 3f0000 18000 183800 0 0 c00300 181800 180000 1c00380 1800180 1800180 3800000 0 6e3000
  //   18000 c06000 c0000 0 c000030 18000 7f000 0 1ffffff8 1800f0e0 3f803c0 3fc07e0 1ffffff0 7e000 7c000
  //   f8001f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
  //   contents of rom_22 (hex, n*v repeats v):
  //   0 1c000000 3c00000 4*0 308000 1c000 0 0 c3000 5*0 400 600000 180 1800000 18c0 3180000 1800 100000
  //   1a00 d80000 18c00 218000 1fc00 7f0000 18000 301c00 0 0 1800180 c3800 380000 1c00380 1800300 1800180
  //   1800000 0 73000 18000 c06000 180000 0 c000070 18000 3c000 1ffffff8 ffffff0 3fc0 0 0 c0000 3fc00
  //   3ec000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
  //   contents of rom_23 (hex, n*v repeats v):
  //   0 f000000 7e00000 4*0 200000 e000 0 0 c3000 5*0 400 600000 180 3000000 cc0 3300000 1800 100000 1a00
  //   d80000 18600 618000 1fc00 7f0000 18000 600e00 38000 38000 1800180 c3000 300000 1c00380 c00300
  //   1800180 e00000 3c003c0 73000 18000 180c000 300000 0 6000060 18000 18000 ffffff0 0 f00 0 0 180000
  //   31f80 1f0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
  //   contents of rom_24 (hex, n*v repeats v):
  //   0 3c00000 c200000 5*0 7000 0 0 c3000 5*0 400 600000 c0 3000000 c60 6300000 1800 100000 1a00 d80000
  //   18600 e18000 1fe00 7f0000 18000 c00700 7c000 7c000 1000180 67000 600040 1c00380 e00600 1800180
  //   7fff80 3c007c0 3f000 18000 180c000 600000 0 70000e0 38000 18000 5*0 300000 303f0 f80c000 fc000 3f000
  //   0 7e0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
  //   contents of rom_25 (hex, n*v repeats v):
  //   0 1e00000 c300000 5*0 7800 0 0 c3000 5*0 400 600000 c0 6000000 660 6600000 1800 100000 1a00 d80000
  //   18300 c18000 1fe00 ff0000 18000 1800380 7c000 7c000 30000c0 66000 c000c0 1c00380 7c3c00 1800180
  //   3fffc0 7e007c0 1e000 18000 3018000 c00000 0 38001c0 30000 18000 5*0 300000 30078 1e00c000 1f800
  //   f8000 0 7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
  //   contents of rom_26 (hex, n*v repeats v):
  //   0 e00000 c300000 5*0 3800 0 0 c3000 5*0 600 c00000 60 6000000 660 c600000 1800 100000 1a00 d80000
  //   18300 1818000 1ff00 1ff0000 0 30001c0 7c000 3c000 30000c0 3e000 1c00180 1c00380 1ff800 1800180 0
  //   3c007c0 e000 18000 7018000 3800000 0 1c00380 30000 30000 0 ffffff0 0 0 0 600000 30000 c000 3f00
  //   7c0000 0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
  //   contents of rom_27 (hex, n*v repeats v):
  //   0 e00000 6600000 5*0 1000 0 0 c3000 5*0 300 1800000 60 c000000 330 cc00000 1800 100000 1a00 fd80000
  //   18180 3818000 1ff80 1ff0000 0 80 38000 38000 6000060 3c000 1ffff80 1c00380 7c000 1800180 0 1800380
  //   e000 18000 6030000 7000000 0 f00f00 330000 3b0000 0 ffffff0 0 0 0 c00000 30000 c000 7e0 3e00000 0
  //   3c0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
  //   contents of rom_28 (hex, n*v repeats v):
  //   0 600000 3c00000 8*0 c3000 5*0 180 3000000 60 c000000 330 18c00000 1800 100000 1a00 fd80000 180c0
  //   3018000 1ff80 3ff0000 7ffffe0 0 0 0 6000060 1c000 3ffff80 ff01ff0 4*0 4000 ffffff0 6030000 fffffe0 0
  //   3ffc00 330000 3f0000 5*0 400000 30000 c000 f0 7000000 0 0 0 1ff800 18000 0 0 0 1fc00 dff800 c1ff830
  //   1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
  //   contents of rom_29 (hex, n*v repeats v):
  //   0 600000 1000000 8*0 c3000 5*0 c0 6000000 30 18000000 198 19800000 1800 100000 1a00 c180000 18060
  //   7ff8000 1ffc0 7ff0000 7ffffe0 0 0 0 c000030 18000 7ffff80 ff01ff0 9*0 ff000 3e0000 3e0000 6*0 30000
  //   c000 10 4*0 fe000 18000 4*0 7e000 18018010 0 0 3c0f0 1c7000 0 1800180 1800180 7e000 3c000 3c000
  //   18000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
  //   contents of rom_30 (hex, n*v repeats v):
  //   11*0 c3000 5*0 40 0 10 8000000 108 10800000 1800 ff00000 1e00 ff80000 1fff0 fff8000 1ffe0 7ff0000
  //   4*0 20 8000 12*0 80000 14*0 18000 5*0 18000 4*0 fe000 0 1000080 1000080 12*0 18000 58*0 f00700
  //   9*e00f00 39*0 8000000 0 0 200000 11*0 3000000 4*0 1ffc00 16*0 700 9*0 7ff0 380 7fe0000 9*0 3ff800 0
  //   0 ff000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
  //   contents of rom_31 (hex, n*v repeats v):
  //   24*0 7f00000 e00 7f00000 0 0 ffe0 7fe0000 119*0 10*3ffc00 54*0 6000000 4*0 3c000 26*0 7ff0 0 ffe0000
  //   9*0 1fe000 0 0 7e0000 5*0 7e0000 7f00 7*0 3c0000 0 0 10000 271*0 38000 0 60000000 70000000 77*0
  //   300000 56*0 38700000 22*0 80000 44*0 3c000 3c000 0 0 3c000 3c000 0 0 10*3c000 8*0 24*3c000 8*0
  //   16*3c000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
  //   contents of rom_32 (hex, n*v repeats v):
  //   150*0 10*7e000 88*0 7fc0000 0 ffffffff 16*0 7e0000 3e00 282*0 10000 0 60000000 70000000 134*0
  //   1fe00000 67*0 3c000 3c000 0 0 3c000 3c000 0 0 10*3c000 8*0 24*3c000 8*0 16*3c000 25*0 3c00 fc0ffff
  //   556*0 1000000 11*0 4 17*0 800000 800000 10*0 80000 4*0 400000 29*0 200000 20*0 20000 0 0 2000 19*0
  //   40000 22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
  //   contents of rom_33 (hex, n*v repeats v):
  //   5*0 3c000 181800 0 c0000 0 0 c3000 0 300 c00000 1c300 c30000 600 600000 c0 6000000 660 6600000 1800
  //   100000 1a00 d80000 18300 c18000 1ff00 ff0000 18000 1800380 7c000 7e000 66000 6000060 1c00080 1c00380
  //   1800180 7ffe00 3fffc0 3e007c0 300 18000 380c0 e0 7e000 3800180 c000 c000 0 1800f80 0 0 0 c00 30038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
endmodule

module \例_32_32汉字显示电路  (
);

  wire \时钟_out ;
  wire [3:0] counter_1_q;
  wire [6:0] \例_机内转区位码_1_位号 , \例_机内转区位码_1_区号 ;
  wire [15:0] rom_1_data;
  wire [31:0] \例_32_32点阵字库_1_out_3 , \例_32_32点阵字库_1_out_4 , \例_32_32点阵字库_1_out_5 , \例_32_32点阵字库_1_out_6 ,
       \例_32_32点阵字库_1_out_7 , \例_32_32点阵字库_1_out_8 , \例_32_32点阵字库_1_out_9 , \例_32_32点阵字库_1_out_10 ,
       \例_32_32点阵字库_1_out_11 , \例_32_32点阵字库_1_out_12 , \例_32_32点阵字库_1_out_13 , \例_32_32点阵字库_1_out_14 ,
       \例_32_32点阵字库_1_out_15 , \例_32_32点阵字库_1_out_16 , \例_32_32点阵字库_1_out_17 , \例_32_32点阵字库_1_out_18 ,
       \例_32_32点阵字库_1_out_19 , \例_32_32点阵字库_1_out_20 , \例_32_32点阵字库_1_out_21 , \例_32_32点阵字库_1_out_22 ,
       \例_32_32点阵字库_1_out_23 , \例_32_32点阵字库_1_out_24 , \例_32_32点阵字库_1_out_25 , \例_32_32点阵字库_1_out_26 ,
       \例_32_32点阵字库_1_out_27 , \例_32_32点阵字库_1_out_28 , \例_32_32点阵字库_1_out_29 , \例_32_32点阵字库_1_out_30 ,
       \例_32_32点阵字库_1_out_31 , \例_32_32点阵字库_1_out_32 , \例_32_32点阵字库_1_out_33 , \例_32_32点阵字库_1_out_34 ;

  Counter #(.width(4), .max('hf)) counter_1 (.Q(counter_1_q), .clk(\时钟_out ));  // open: load, D, count, carry, clr
  Clock \u_时钟  (.out(\时钟_out ));
  ROM #(.addrWidth(4), .dataWidth(16)) rom_1 (.addr(counter_1_q), .data(rom_1_data));  // open: sel
  \例_机内转区位码  \u_例_机内转区位码_1  (.\位号 (\例_机内转区位码_1_位号 ), .\区号 (\例_机内转区位码_1_区号 ), .GB2312(rom_1_data));
  DotMatrix #(.inputtype("row"), .matrixcols(32), .matrixrows(32), .dotshape("circle")) dotmatrix_1 (
    .row0(\例_32_32点阵字库_1_out_3 ), .row1(\例_32_32点阵字库_1_out_4 ), .row2(\例_32_32点阵字库_1_out_5 ),
    .row3(\例_32_32点阵字库_1_out_6 ), .row4(\例_32_32点阵字库_1_out_7 ), .row5(\例_32_32点阵字库_1_out_8 ),
    .row6(\例_32_32点阵字库_1_out_9 ), .row7(\例_32_32点阵字库_1_out_10 ), .row8(\例_32_32点阵字库_1_out_11 ),
    .row9(\例_32_32点阵字库_1_out_12 ), .row10(\例_32_32点阵字库_1_out_13 ), .row11(\例_32_32点阵字库_1_out_14 ),
    .row12(\例_32_32点阵字库_1_out_15 ), .row13(\例_32_32点阵字库_1_out_16 ), .row14(\例_32_32点阵字库_1_out_17 ),
    .row15(\例_32_32点阵字库_1_out_18 ), .row16(\例_32_32点阵字库_1_out_19 ), .row17(\例_32_32点阵字库_1_out_20 ),
    .row18(\例_32_32点阵字库_1_out_21 ), .row19(\例_32_32点阵字库_1_out_22 ), .row20(\例_32_32点阵字库_1_out_23 ),
    .row21(\例_32_32点阵字库_1_out_24 ), .row22(\例_32_32点阵字库_1_out_25 ), .row23(\例_32_32点阵字库_1_out_26 ),
    .row24(\例_32_32点阵字库_1_out_27 ), .row25(\例_32_32点阵字库_1_out_28 ), .row26(\例_32_32点阵字库_1_out_29 ),
    .row27(\例_32_32点阵字库_1_out_30 ), .row28(\例_32_32点阵字库_1_out_31 ), .row29(\例_32_32点阵字库_1_out_32 ),
    .row30(\例_32_32点阵字库_1_out_33 ), .row31(\例_32_32点阵字库_1_out_34 ));
  \例_32_32点阵字库  \u_例_32_32点阵字库_1  (
    .out_3(\例_32_32点阵字库_1_out_3 ), .out_4(\例_32_32点阵字库_1_out_4 ), .out_5(\例_32_32点阵字库_1_out_5 ),
    .out_6(\例_32_32点阵字库_1_out_6 ), .out_7(\例_32_32点阵字库_1_out_7 ), .out_8(\例_32_32点阵字库_1_out_8 ),
    .out_9(\例_32_32点阵字库_1_out_9 ), .out_10(\例_32_32点阵字库_1_out_10 ), .out_11(\例_32_32点阵字库_1_out_11 ),
    .out_12(\例_32_32点阵字库_1_out_12 ), .out_13(\例_32_32点阵字库_1_out_13 ), .out_14(\例_32_32点阵字库_1_out_14 ),
    .out_15(\例_32_32点阵字库_1_out_15 ), .out_16(\例_32_32点阵字库_1_out_16 ), .out_17(\例_32_32点阵字库_1_out_17 ),
    .out_18(\例_32_32点阵字库_1_out_18 ), .out_19(\例_32_32点阵字库_1_out_19 ), .out_20(\例_32_32点阵字库_1_out_20 ),
    .out_21(\例_32_32点阵字库_1_out_21 ), .out_22(\例_32_32点阵字库_1_out_22 ), .out_23(\例_32_32点阵字库_1_out_23 ),
    .out_24(\例_32_32点阵字库_1_out_24 ), .out_25(\例_32_32点阵字库_1_out_25 ), .out_26(\例_32_32点阵字库_1_out_26 ),
    .out_27(\例_32_32点阵字库_1_out_27 ), .out_28(\例_32_32点阵字库_1_out_28 ), .out_29(\例_32_32点阵字库_1_out_29 ),
    .out_30(\例_32_32点阵字库_1_out_30 ), .out_31(\例_32_32点阵字库_1_out_31 ), .out_32(\例_32_32点阵字库_1_out_32 ),
    .out_33(\例_32_32点阵字库_1_out_33 ), .out_34(\例_32_32点阵字库_1_out_34 ), .\区号 (\例_机内转区位码_1_区号 ),
    .\位号 (\例_机内转区位码_1_位号 ));

  // Notes on the sheet:
  //   计数器
  //   GB2312
  //   实现国标转区位码电路，使得系统每个时钟正确显示一个汉字
  //   请将下面这段文字转换成GB2312替换ROM存储器中内容
  //   contents of rom_1 (hex, n*v repeats v):
  //   3128 2316 3929 a3b2 a3b0 a3b4 a3b8 2316 ff11
endmodule
